// Logisim project TPU.circ as structural Verilog: 27 circuits, main circuit adder_2bit
module ins_4x4_Gausian (
);

  wire clock_1_out, nor_1_out, not_1_out, not_2_out, or_1_out, or_2_out, register_2_q;
  wire [3:0] ins_splitter_1_dimension, ins_splitter_1_opcode;
  wire [7:0] adder_1_out, bit_extender_1_out, counter_1_q, counter_2_q, counter_3_q, counter_4_q,
       counter_5_q, ins_splitter_1_adress, multiplier_1_out;
  wire [15:0] Instruction_Ram_dout, matmult_4x4_1_element, PCU_data, RamA_dout, RamB_dout, register_1_q,
       registerbanks_4_1_out1, registerbanks_4_1_out2, registerbanks_4_1_out3, registerbanks_4_1_out4,
       registerbanks_4_2_out1, registerbanks_4_2_out2, registerbanks_4_2_out3, registerbanks_4_2_out4;

  not not_1 (not_1_out, or_1_out);
  not not_2 (not_2_out, or_2_out);
  Clock clock_1 (.out(clock_1_out));
  RAM #(.dataWidth(16), .\type ("nonvolatile")) RamA (
    .addr(counter_1_q), .clk(clock_1_out), .dout(RamA_dout));  // open: we, oe, din
  Counter counter_1 (
    .load(not_1_out), .D(ins_splitter_1_adress), .count(or_1_out), .Q(counter_1_q), .clk(clock_1_out));  // open: carry, up, clr
  RAM #(.dataWidth(16)) RamB (.addr(counter_2_q), .clk(clock_1_out), .dout(RamB_dout));  // open: we, oe, din
  Counter counter_2 (
    .load(not_2_out), .D(ins_splitter_1_adress), .count(or_2_out), .Q(counter_2_q), .clk(clock_1_out));  // open: carry, up, clr
  RAM #(.dataWidth(16)) Instruction_Ram (
    .addr(counter_3_q), .clk(clock_1_out), .dout(Instruction_Ram_dout));  // open: we, oe, din
  Counter counter_3 (.count(nor_1_out), .Q(counter_3_q), .clk(clock_1_out));  // open: load, D, carry, up, clr
  nor nor_1 (nor_1_out, PCU_data[0], PCU_data[1], PCU_data[9], PCU_data[8], PCU_data[7], PCU_data[6], PCU_data[5], PCU_data[4], PCU_data[3], PCU_data[2]);
  or or_1 (or_1_out, PCU_data[9], PCU_data[8], PCU_data[7], PCU_data[6]);
  or or_2 (or_2_out, PCU_data[5], PCU_data[4], PCU_data[3], PCU_data[2]);
  Ins_splitter ins_splitter_1 (
    .Instruction(Instruction_Ram_dout), .Clock(clock_1_out), .Adress(ins_splitter_1_adress),
    .Dimension(ins_splitter_1_dimension), .Opcode(ins_splitter_1_opcode));  // open: WE
  assign bit_extender_1_out = {{4{ins_splitter_1_opcode[3]}}, ins_splitter_1_opcode};  // Bit_Extender bit_extender_1
  Multiplier multiplier_1 (.a(bit_extender_1_out), .b(8'ha), .out(multiplier_1_out));  // open: cin, cout
  Counter counter_4 (.Q(counter_4_q), .clk(clock_1_out), .clr(register_2_q));  // open: load, D, count, carry, up
  Adder adder_1 (.a(counter_4_q), .b(multiplier_1_out), .out(adder_1_out));  // open: cin, cout
  registerBanks_4 registerbanks_4_1 (
    .value(RamA_dout), .WE1(PCU_data[9]), .WE2(PCU_data[8]), .WE3(PCU_data[7]), .WE4(PCU_data[6]),
    .clock(clock_1_out), .out1(registerbanks_4_1_out1), .out2(registerbanks_4_1_out2),
    .out3(registerbanks_4_1_out3), .out4(registerbanks_4_1_out4));  // open: reset
  registerBanks_4 registerbanks_4_2 (
    .value(RamB_dout), .WE1(PCU_data[5]), .WE2(PCU_data[4]), .WE3(PCU_data[3]), .WE4(PCU_data[2]),
    .clock(clock_1_out), .out1(registerbanks_4_2_out1), .out2(registerbanks_4_2_out2),
    .out3(registerbanks_4_2_out3), .out4(registerbanks_4_2_out4));  // open: reset
  ROM #(.dataWidth(16)) PCU (.addr(adder_1_out), .data(PCU_data));
  matMult_4x4 matmult_4x4_1 (
    .row1(registerbanks_4_1_out1), .row2(registerbanks_4_1_out2), .row3(registerbanks_4_1_out3),
    .row4(registerbanks_4_1_out4), .col1(registerbanks_4_2_out1), .col2(registerbanks_4_2_out2),
    .col3(registerbanks_4_2_out3), .col4(registerbanks_4_2_out4), .Element(matmult_4x4_1_element));  // open: carryout
  Register #(.width(16)) register_1 (
    .D(matmult_4x4_1_element), .en(PCU_data[1]), .clk(clock_1_out), .Q(register_1_q));  // open: clr
  Register #(.width(1)) register_2 (
    .D(PCU_data[15]), .en(clock_1_out), .clk(clock_1_out), .Q(register_2_q));  // open: clr
  RAM #(.dataWidth(16)) RamC (
    .addr(counter_5_q), .we(PCU_data[0]), .clk(clock_1_out), .din(register_1_q));  // open: oe, dout
  Counter counter_5 (.count(PCU_data[0]), .Q(counter_5_q), .clk(clock_1_out));  // open: load, D, carry, up, clr

  // Notes on the sheet:
  //   Load A
  //   Load B
  //   MatMult
  //   Store C
endmodule

module matmult_systrolicTiling8x8 (
);

  wire clock_1_out, or_1_out, or_2_out;
  wire [3:0] counter_3_q, counter_3_q_2;
  wire [7:0] counter_1_q, counter_2_q, counter_4_q;
  wire [15:0] A1_q, A2_q, A3_q, A4_q, B1_q, B2_q, B3_q, B4_q, C1_q, C2_q, C3_q, C4_q, C5_q, C6_q, C7_q, C8_q,
       C9_q, C10_q, C11_q, C12_q, C13_q, C14_q, C15_q, C16_q, controlled_buffer_1_out, ram_1_dout,
       ram_2_dout, register_1_q, systrolic_4x4gausian_1_c1, systrolic_4x4gausian_1_c2,
       systrolic_4x4gausian_1_c3, systrolic_4x4gausian_1_c4, systrolic_4x4gausian_1_c5,
       systrolic_4x4gausian_1_c6, systrolic_4x4gausian_1_c7, systrolic_4x4gausian_1_c8,
       systrolic_4x4gausian_1_c9, systrolic_4x4gausian_1_c10, systrolic_4x4gausian_1_c11,
       systrolic_4x4gausian_1_c12, systrolic_4x4gausian_1_c13, systrolic_4x4gausian_1_c14,
       systrolic_4x4gausian_1_c15, systrolic_4x4gausian_1_c16;
  wire [23:0] rom_1_data;

  or or_1 (or_1_out, rom_1_data[23], rom_1_data[22], rom_1_data[21], rom_1_data[20]);
  Counter counter_1 (.count(or_1_out), .Q(counter_1_q), .clk(clock_1_out));  // open: load, D, carry, up, clr
  Counter counter_2 (.count(or_1_out), .Q(counter_2_q), .clk(clock_1_out));  // open: load, D, carry, up, clr
  Clock clock_1 (.out(clock_1_out));
  RAM #(.dataWidth(16)) ram_1 (.addr(counter_1_q), .clk(clock_1_out), .dout(ram_1_dout));  // open: we, oe, din
  RAM #(.dataWidth(16)) ram_2 (.addr(counter_2_q), .clk(clock_1_out), .dout(ram_2_dout));  // open: we, oe, din
  Register #(.width(16)) A1 (.D(ram_1_dout), .en(rom_1_data[23]), .clk(clock_1_out), .Q(A1_q));  // open: clr
  Register #(.width(16)) A2 (.D(ram_1_dout), .en(rom_1_data[22]), .clk(clock_1_out), .Q(A2_q));  // open: clr
  Register #(.width(16)) A3 (.D(ram_1_dout), .en(rom_1_data[21]), .clk(clock_1_out), .Q(A3_q));  // open: clr
  Register #(.width(16)) A4 (.D(ram_1_dout), .en(rom_1_data[20]), .clk(clock_1_out), .Q(A4_q));  // open: clr
  Register #(.width(16)) B1 (.D(ram_2_dout), .en(rom_1_data[23]), .clk(clock_1_out), .Q(B1_q));  // open: clr
  Register #(.width(16)) B2 (.D(ram_2_dout), .en(rom_1_data[22]), .clk(clock_1_out), .Q(B2_q));  // open: clr
  Register #(.width(16)) B3 (.D(ram_2_dout), .en(rom_1_data[21]), .clk(clock_1_out), .Q(B3_q));  // open: clr
  Register #(.width(16)) B4 (.D(ram_2_dout), .en(rom_1_data[20]), .clk(clock_1_out), .Q(B4_q));  // open: clr
  systrolic_4x4Gausian systrolic_4x4gausian_1 (
    .B1(B1_q), .B2(B2_q), .B3(B3_q), .B4(B4_q), .A1(A1_q), .A2(A2_q), .A3(A3_q), .A4(A4_q),
    .Clock(clock_1_out), .C1(systrolic_4x4gausian_1_c1), .C2(systrolic_4x4gausian_1_c2),
    .C3(systrolic_4x4gausian_1_c3), .C4(systrolic_4x4gausian_1_c4), .C5(systrolic_4x4gausian_1_c5),
    .C6(systrolic_4x4gausian_1_c6), .C7(systrolic_4x4gausian_1_c7), .C8(systrolic_4x4gausian_1_c8),
    .C9(systrolic_4x4gausian_1_c9), .C10(systrolic_4x4gausian_1_c10), .C11(systrolic_4x4gausian_1_c11),
    .C12(systrolic_4x4gausian_1_c12), .C13(systrolic_4x4gausian_1_c13), .C14(systrolic_4x4gausian_1_c14),
    .C15(systrolic_4x4gausian_1_c15), .C16(systrolic_4x4gausian_1_c16));
  Register #(.width(16)) C1 (.D(systrolic_4x4gausian_1_c1), .Q(C1_q));  // open: en, clk, clr
  Register #(.width(16)) C3 (.D(systrolic_4x4gausian_1_c3), .Q(C3_q));  // open: en, clk, clr
  Register #(.width(16)) C5 (.D(systrolic_4x4gausian_1_c5), .Q(C5_q));  // open: en, clk, clr
  Register #(.width(16)) C7 (.D(systrolic_4x4gausian_1_c7), .Q(C7_q));  // open: en, clk, clr
  Register #(.width(16)) C9 (.D(systrolic_4x4gausian_1_c9), .Q(C9_q));  // open: en, clk, clr
  Register #(.width(16)) C11 (.D(systrolic_4x4gausian_1_c11), .Q(C11_q));  // open: en, clk, clr
  Register #(.width(16)) C13 (.D(systrolic_4x4gausian_1_c13), .Q(C13_q));  // open: en, clk, clr
  Register #(.width(16)) C15 (.D(systrolic_4x4gausian_1_c15), .Q(C15_q));  // open: en, clk, clr
  Register #(.width(16)) C2 (.D(systrolic_4x4gausian_1_c2), .Q(C2_q));  // open: en, clk, clr
  Register #(.width(16)) C4 (.D(systrolic_4x4gausian_1_c4), .Q(C4_q));  // open: en, clk, clr
  Register #(.width(16)) C6 (.D(systrolic_4x4gausian_1_c6), .Q(C6_q));  // open: en, clk, clr
  Register #(.width(16)) C8 (.D(systrolic_4x4gausian_1_c8), .Q(C8_q));  // open: en, clk, clr
  Register #(.width(16)) C10 (.D(systrolic_4x4gausian_1_c10), .Q(C10_q));  // open: en, clk, clr
  Register #(.width(16)) C12 (.D(systrolic_4x4gausian_1_c12), .Q(C12_q));  // open: en, clk, clr
  Register #(.width(16)) C14 (.D(systrolic_4x4gausian_1_c14), .Q(C14_q));  // open: en, clk, clr
  Register #(.width(16)) C16 (.D(systrolic_4x4gausian_1_c16), .Q(C16_q));  // open: en, clk, clr
  assign controlled_buffer_1_out = rom_1_data[19] ? C1_q : 16'bz;  // Controlled_Buffer controlled_buffer_1
  assign controlled_buffer_1_out = rom_1_data[18] ? C2_q : 16'bz;  // Controlled_Buffer controlled_buffer_2
  assign controlled_buffer_1_out = rom_1_data[17] ? C3_q : 16'bz;  // Controlled_Buffer controlled_buffer_3
  Hex_Digit_Display hex_digit_display_1 (.value(counter_3_q_2));  // open: dp
  Hex_Digit_Display hex_digit_display_2 (.value(counter_3_q));  // open: dp
  assign controlled_buffer_1_out = rom_1_data[16] ? C4_q : 16'bz;  // Controlled_Buffer controlled_buffer_4
  assign controlled_buffer_1_out = rom_1_data[15] ? C5_q : 16'bz;  // Controlled_Buffer controlled_buffer_5
  assign controlled_buffer_1_out = rom_1_data[14] ? C6_q : 16'bz;  // Controlled_Buffer controlled_buffer_6
  assign controlled_buffer_1_out = rom_1_data[13] ? C7_q : 16'bz;  // Controlled_Buffer controlled_buffer_7
  assign controlled_buffer_1_out = rom_1_data[12] ? C8_q : 16'bz;  // Controlled_Buffer controlled_buffer_8
  assign controlled_buffer_1_out = rom_1_data[11] ? C9_q : 16'bz;  // Controlled_Buffer controlled_buffer_9
  assign controlled_buffer_1_out = rom_1_data[10] ? C10_q : 16'bz;  // Controlled_Buffer controlled_buffer_10
  assign controlled_buffer_1_out = rom_1_data[9] ? C11_q : 16'bz;  // Controlled_Buffer controlled_buffer_11
  assign controlled_buffer_1_out = rom_1_data[8] ? C12_q : 16'bz;  // Controlled_Buffer controlled_buffer_12
  assign controlled_buffer_1_out = rom_1_data[7] ? C13_q : 16'bz;  // Controlled_Buffer controlled_buffer_13
  assign controlled_buffer_1_out = rom_1_data[6] ? C14_q : 16'bz;  // Controlled_Buffer controlled_buffer_14
  assign controlled_buffer_1_out = rom_1_data[5] ? C15_q : 16'bz;  // Controlled_Buffer controlled_buffer_15
  assign controlled_buffer_1_out = rom_1_data[4] ? C16_q : 16'bz;  // Controlled_Buffer controlled_buffer_16
  or or_2 (or_2_out, rom_1_data[4], rom_1_data[5], rom_1_data[6], rom_1_data[7], rom_1_data[8], rom_1_data[9], rom_1_data[10], rom_1_data[11], rom_1_data[12], rom_1_data[13], rom_1_data[14], rom_1_data[15], rom_1_data[16], rom_1_data[17], rom_1_data[18], rom_1_data[19]);
  Counter counter_3 (.Q({counter_3_q_2, counter_3_q}), .clk(clock_1_out));  // open: load, D, count, carry, up, clr
  Register #(.width(16)) register_1 (
    .D(controlled_buffer_1_out), .en(or_2_out), .clk(clock_1_out), .Q(register_1_q));  // open: clr
  ROM #(.dataWidth(24)) rom_1 (.addr({counter_3_q_2, counter_3_q}), .data(rom_1_data));
  RAM #(.dataWidth(16)) ram_3 (
    .addr(counter_4_q), .we(rom_1_data[3]), .clk(clock_1_out), .din(register_1_q));  // open: oe, dout
  Counter counter_4 (.count(rom_1_data[3]), .Q(counter_4_q), .clk(clock_1_out));  // open: load, D, carry, up, clr
endmodule

module matmult_systrolicRNC4x4 (
);

  wire clock_1_out, or_1_out, or_2_out;
  wire [3:0] counter_3_q, counter_3_q_2;
  wire [7:0] counter_1_q, counter_2_q, counter_4_q;
  wire [15:0] A1_q, A2_q, A3_q, A4_q, B1_q, B2_q, B3_q, B4_q, C1_q, C2_q, C3_q, C4_q, C5_q, C6_q, C7_q, C8_q,
       C9_q, C10_q, C11_q, C12_q, C13_q, C14_q, C15_q, C16_q, controlled_buffer_1_out, ram_1_dout,
       ram_2_dout, register_1_q, systrolic_4x4gausian_1_c1, systrolic_4x4gausian_1_c2,
       systrolic_4x4gausian_1_c3, systrolic_4x4gausian_1_c4, systrolic_4x4gausian_1_c5,
       systrolic_4x4gausian_1_c6, systrolic_4x4gausian_1_c7, systrolic_4x4gausian_1_c8,
       systrolic_4x4gausian_1_c9, systrolic_4x4gausian_1_c10, systrolic_4x4gausian_1_c11,
       systrolic_4x4gausian_1_c12, systrolic_4x4gausian_1_c13, systrolic_4x4gausian_1_c14,
       systrolic_4x4gausian_1_c15, systrolic_4x4gausian_1_c16;
  wire [23:0] rom_1_data;

  or or_1 (or_1_out, rom_1_data[23], rom_1_data[22], rom_1_data[21], rom_1_data[20]);
  Counter counter_1 (.count(or_1_out), .Q(counter_1_q), .clk(clock_1_out));  // open: load, D, carry, up, clr
  Counter counter_2 (.count(or_1_out), .Q(counter_2_q), .clk(clock_1_out));  // open: load, D, carry, up, clr
  Clock clock_1 (.out(clock_1_out));
  RAM #(.dataWidth(16)) ram_1 (.addr(counter_1_q), .clk(clock_1_out), .dout(ram_1_dout));  // open: we, oe, din
  RAM #(.dataWidth(16)) ram_2 (.addr(counter_2_q), .clk(clock_1_out), .dout(ram_2_dout));  // open: we, oe, din
  Register #(.trigger("falling"), .width(16)) A1 (
    .D(ram_1_dout), .en(rom_1_data[23]), .clk(clock_1_out), .Q(A1_q));  // open: clr
  Register #(.trigger("falling"), .width(16)) A2 (
    .D(ram_1_dout), .en(rom_1_data[22]), .clk(clock_1_out), .Q(A2_q));  // open: clr
  Register #(.trigger("falling"), .width(16)) A3 (
    .D(ram_1_dout), .en(rom_1_data[21]), .clk(clock_1_out), .Q(A3_q));  // open: clr
  Register #(.trigger("falling"), .width(16)) A4 (
    .D(ram_1_dout), .en(rom_1_data[20]), .clk(clock_1_out), .Q(A4_q));  // open: clr
  Register #(.trigger("falling"), .width(16)) B1 (
    .D(ram_2_dout), .en(rom_1_data[23]), .clk(clock_1_out), .Q(B1_q));  // open: clr
  Register #(.trigger("falling"), .width(16)) B2 (
    .D(ram_2_dout), .en(rom_1_data[22]), .clk(clock_1_out), .Q(B2_q));  // open: clr
  Register #(.trigger("falling"), .width(16)) B3 (
    .D(ram_2_dout), .en(rom_1_data[21]), .clk(clock_1_out), .Q(B3_q));  // open: clr
  Register #(.trigger("falling"), .width(16)) B4 (
    .D(ram_2_dout), .en(rom_1_data[20]), .clk(clock_1_out), .Q(B4_q));  // open: clr
  systrolic_4x4Gausian systrolic_4x4gausian_1 (
    .B1(B1_q), .B2(B2_q), .B3(B3_q), .B4(B4_q), .A1(A1_q), .A2(A2_q), .A3(A3_q), .A4(A4_q),
    .Clock(clock_1_out), .C1(systrolic_4x4gausian_1_c1), .C2(systrolic_4x4gausian_1_c2),
    .C3(systrolic_4x4gausian_1_c3), .C4(systrolic_4x4gausian_1_c4), .C5(systrolic_4x4gausian_1_c5),
    .C6(systrolic_4x4gausian_1_c6), .C7(systrolic_4x4gausian_1_c7), .C8(systrolic_4x4gausian_1_c8),
    .C9(systrolic_4x4gausian_1_c9), .C10(systrolic_4x4gausian_1_c10), .C11(systrolic_4x4gausian_1_c11),
    .C12(systrolic_4x4gausian_1_c12), .C13(systrolic_4x4gausian_1_c13), .C14(systrolic_4x4gausian_1_c14),
    .C15(systrolic_4x4gausian_1_c15), .C16(systrolic_4x4gausian_1_c16));
  Register #(.width(16)) C1 (.D(systrolic_4x4gausian_1_c1), .en(1'b1), .clk(clock_1_out), .Q(C1_q));  // open: clr
  Register #(.width(16)) C3 (.D(systrolic_4x4gausian_1_c3), .en(1'b1), .clk(clock_1_out), .Q(C3_q));  // open: clr
  Register #(.width(16)) C5 (.D(systrolic_4x4gausian_1_c5), .en(1'b1), .clk(clock_1_out), .Q(C5_q));  // open: clr
  Register #(.width(16)) C7 (.D(systrolic_4x4gausian_1_c7), .en(1'b1), .clk(clock_1_out), .Q(C7_q));  // open: clr
  Register #(.width(16)) C9 (.D(systrolic_4x4gausian_1_c9), .en(1'b1), .clk(clock_1_out), .Q(C9_q));  // open: clr
  Register #(.width(16)) C11 (.D(systrolic_4x4gausian_1_c11), .en(1'b1), .clk(clock_1_out), .Q(C11_q));  // open: clr
  Register #(.width(16)) C13 (.D(systrolic_4x4gausian_1_c13), .en(1'b1), .clk(clock_1_out), .Q(C13_q));  // open: clr
  Register #(.width(16)) C15 (.D(systrolic_4x4gausian_1_c15), .en(1'b1), .clk(clock_1_out), .Q(C15_q));  // open: clr
  Register #(.width(16)) C2 (.D(systrolic_4x4gausian_1_c2), .en(1'b1), .clk(clock_1_out), .Q(C2_q));  // open: clr
  Register #(.width(16)) C4 (.D(systrolic_4x4gausian_1_c4), .en(1'b1), .clk(clock_1_out), .Q(C4_q));  // open: clr
  Register #(.width(16)) C6 (.D(systrolic_4x4gausian_1_c6), .en(1'b1), .clk(clock_1_out), .Q(C6_q));  // open: clr
  Register #(.width(16)) C8 (.D(systrolic_4x4gausian_1_c8), .en(1'b1), .clk(clock_1_out), .Q(C8_q));  // open: clr
  Register #(.width(16)) C10 (.D(systrolic_4x4gausian_1_c10), .en(1'b1), .clk(clock_1_out), .Q(C10_q));  // open: clr
  Register #(.width(16)) C12 (.D(systrolic_4x4gausian_1_c12), .en(1'b1), .clk(clock_1_out), .Q(C12_q));  // open: clr
  Register #(.width(16)) C14 (.D(systrolic_4x4gausian_1_c14), .en(1'b1), .clk(clock_1_out), .Q(C14_q));  // open: clr
  Register #(.width(16)) C16 (.D(systrolic_4x4gausian_1_c16), .en(1'b1), .clk(clock_1_out), .Q(C16_q));  // open: clr
  assign controlled_buffer_1_out = rom_1_data[19] ? C1_q : 16'bz;  // Controlled_Buffer controlled_buffer_1
  assign controlled_buffer_1_out = rom_1_data[18] ? C2_q : 16'bz;  // Controlled_Buffer controlled_buffer_2
  assign controlled_buffer_1_out = rom_1_data[17] ? C3_q : 16'bz;  // Controlled_Buffer controlled_buffer_3
  Hex_Digit_Display hex_digit_display_1 (.value(counter_3_q_2));  // open: dp
  Hex_Digit_Display hex_digit_display_2 (.value(counter_3_q));  // open: dp
  assign controlled_buffer_1_out = rom_1_data[16] ? C4_q : 16'bz;  // Controlled_Buffer controlled_buffer_4
  assign controlled_buffer_1_out = rom_1_data[15] ? C5_q : 16'bz;  // Controlled_Buffer controlled_buffer_5
  assign controlled_buffer_1_out = rom_1_data[14] ? C6_q : 16'bz;  // Controlled_Buffer controlled_buffer_6
  assign controlled_buffer_1_out = rom_1_data[13] ? C7_q : 16'bz;  // Controlled_Buffer controlled_buffer_7
  assign controlled_buffer_1_out = rom_1_data[12] ? C8_q : 16'bz;  // Controlled_Buffer controlled_buffer_8
  assign controlled_buffer_1_out = rom_1_data[11] ? C9_q : 16'bz;  // Controlled_Buffer controlled_buffer_9
  assign controlled_buffer_1_out = rom_1_data[10] ? C10_q : 16'bz;  // Controlled_Buffer controlled_buffer_10
  assign controlled_buffer_1_out = rom_1_data[9] ? C11_q : 16'bz;  // Controlled_Buffer controlled_buffer_11
  assign controlled_buffer_1_out = rom_1_data[8] ? C12_q : 16'bz;  // Controlled_Buffer controlled_buffer_12
  assign controlled_buffer_1_out = rom_1_data[7] ? C13_q : 16'bz;  // Controlled_Buffer controlled_buffer_13
  assign controlled_buffer_1_out = rom_1_data[6] ? C14_q : 16'bz;  // Controlled_Buffer controlled_buffer_14
  assign controlled_buffer_1_out = rom_1_data[5] ? C15_q : 16'bz;  // Controlled_Buffer controlled_buffer_15
  assign controlled_buffer_1_out = rom_1_data[4] ? C16_q : 16'bz;  // Controlled_Buffer controlled_buffer_16
  or or_2 (or_2_out, rom_1_data[4], rom_1_data[5], rom_1_data[6], rom_1_data[7], rom_1_data[8], rom_1_data[9], rom_1_data[10], rom_1_data[11], rom_1_data[12], rom_1_data[13], rom_1_data[14], rom_1_data[15], rom_1_data[16], rom_1_data[17], rom_1_data[18], rom_1_data[19]);
  Counter counter_3 (.Q({counter_3_q_2, counter_3_q}), .clk(clock_1_out));  // open: load, D, count, carry, up, clr
  Register #(.width(16)) register_1 (
    .D(controlled_buffer_1_out), .en(or_2_out), .clk(clock_1_out), .Q(register_1_q));  // open: clr
  ROM #(.dataWidth(24)) rom_1 (.addr({counter_3_q_2, counter_3_q}), .data(rom_1_data));
  RAM #(.dataWidth(16)) ram_3 (
    .addr(counter_4_q), .we(rom_1_data[3]), .clk(clock_1_out), .din(register_1_q));  // open: oe, dout
  Counter counter_4 (.count(rom_1_data[3]), .Q(counter_4_q), .clk(clock_1_out));  // open: load, D, carry, up, clr

  // Notes on the sheet:
  //   contents of rom_1 (hex, n*v repeats v):
  //   800000 800000 400000 800000 400000 200000 800000 480000 200008 100000 400000 240000 120008 200008
  //   110000 108008 4008 2008 1008 808 408 208 108 88 48 28 18 8
endmodule

module systrolicMMult_2x2_Gausian (
);

  wire clock_1_out, or_1_out, systrolic_processingelement_1_p5;
  wire [7:0] counter_1_q, counter_2_q, counter_3_q, counter_4_q, counter_5_q, counter_6_q;
  wire [15:0] controlled_buffer_1_out, ram_1_dout, ram_2_dout, ram_3_dout, ram_4_dout, register_1_q,
       rom_1_data, systrolic_processingelement_1_p4, systrolic_processingelement_1_p6,
       systrolic_processingelement_2_p4, systrolic_processingelement_2_p5,
       systrolic_processingelement_3_aout, systrolic_processingelement_3_bout,
       systrolic_processingelement_4_cout;

  Counter counter_1 (.count(rom_1_data[13]), .Q(counter_1_q), .clk(clock_1_out));  // open: load, D, carry, up, clr
  Clock clock_1 (.out(clock_1_out));
  Counter counter_2 (.count(rom_1_data[12]), .Q(counter_2_q), .clk(clock_1_out));  // open: load, D, carry, up, clr
  RAM #(.dataWidth(16), .\type ("nonvolatile")) ram_1 (
    .addr(counter_1_q), .clk(clock_1_out), .dout(ram_1_dout));  // open: we, oe, din
  RAM #(.dataWidth(16), .\type ("nonvolatile")) ram_2 (
    .addr(counter_2_q), .clk(clock_1_out), .dout(ram_2_dout));  // open: we, oe, din
  Counter counter_3 (.Q(counter_3_q), .clk(clock_1_out));  // open: load, D, count, carry, up, clr
  // Probe on ram_1_dout
  // Probe on ram_2_dout
  ROM #(.dataWidth(16)) rom_1 (.addr(counter_3_q), .data(rom_1_data));
  Counter counter_4 (.count(rom_1_data[14]), .Q(counter_4_q), .clk(clock_1_out));  // open: load, D, carry, up, clr
  RAM #(.dataWidth(16), .\type ("nonvolatile")) ram_3 (
    .addr(counter_4_q), .clk(clock_1_out), .dout(ram_3_dout));  // open: we, oe, din
  // Probe on systrolic_processingelement_2_p5
  // Probe on ram_3_dout
  // Systrolic_ProcessingElement systrolic_processingelement_1: pin names not known; wires that end beside it: ram_1_dout, ram_3_dout, clock_1_out, systrolic_processingelement_1_p4, systrolic_processingelement_1_p5, systrolic_processingelement_1_p6
  // Probe on systrolic_processingelement_1_p6
  // Systrolic_ProcessingElement systrolic_processingelement_2: pin names not known; wires that end beside it: ram_2_dout, systrolic_processingelement_1_p5, clock_1_out, systrolic_processingelement_2_p4, systrolic_processingelement_2_p5
  Counter counter_5 (.count(rom_1_data[15]), .Q(counter_5_q), .clk(clock_1_out));  // open: load, D, carry, up, clr
  assign controlled_buffer_1_out = rom_1_data[3] ? systrolic_processingelement_1_p6 : 16'bz;  // Controlled_Buffer controlled_buffer_1
  assign controlled_buffer_1_out = rom_1_data[1] ? systrolic_processingelement_2_p5 : 16'bz;  // Controlled_Buffer controlled_buffer_2
  RAM #(.dataWidth(16), .\type ("nonvolatile")) ram_4 (
    .addr(counter_5_q), .clk(clock_1_out), .dout(ram_4_dout));  // open: we, oe, din
  // Probe on systrolic_processingelement_4_cout
  // Probe on ram_4_dout
  // Probe on systrolic_processingelement_3_aout
  Systrolic_ProcessingElement systrolic_processingelement_3 (
    .Ain(systrolic_processingelement_1_p4), .Bin(ram_4_dout), .Clock(clock_1_out),
    .Aout(systrolic_processingelement_3_aout), .Bout(systrolic_processingelement_3_bout));  // open: Cout
  Systrolic_ProcessingElement systrolic_processingelement_4 (
    .Ain(systrolic_processingelement_2_p4), .Bin(systrolic_processingelement_3_bout), .Clock(clock_1_out),
    .Cout(systrolic_processingelement_4_cout));  // open: Aout, Bout
  assign controlled_buffer_1_out = rom_1_data[0] ? systrolic_processingelement_4_cout : 16'bz;  // Controlled_Buffer controlled_buffer_3
  or or_1 (or_1_out, rom_1_data[0], rom_1_data[1], rom_1_data[2], rom_1_data[3]);
  assign controlled_buffer_1_out = rom_1_data[2] ? systrolic_processingelement_3_aout : 16'bz;  // Controlled_Buffer controlled_buffer_4
  Register #(.width(16)) register_1 (
    .D(controlled_buffer_1_out), .en(or_1_out), .clk(clock_1_out), .Q(register_1_q));  // open: clr
  Counter counter_6 (.count(rom_1_data[7]), .Q(counter_6_q), .clk(clock_1_out));  // open: load, D, carry, up, clr
  RAM #(.dataWidth(16)) ram_5 (
    .addr(counter_6_q), .we(rom_1_data[7]), .clk(clock_1_out), .din(register_1_q));  // open: oe, dout

  // Notes on the sheet:
  //   contents of rom_1 (hex, n*v repeats v):
  //   6000 f008 9082 9084 81 80
endmodule

module matmult_tiling2x2 (
  input  in_1
);

  wire clock_1_out, or_1_out, or_2_out;
  wire [3:0] counter_3_q, counter_3_q_2;
  wire [7:0] counter_1_q, counter_2_q, counter_4_q;
  wire [15:0] A1_q, A2_q, A3_q, A4_q, adder_1_out, B1_q, B2_q, B3_q, B4_q, controlled_buffer_1_out,
       controlled_buffer_2_out, controlled_buffer_3_out, controlled_buffer_4_out, controlled_buffer_5_out,
       controlled_buffer_6_out, controlled_buffer_7_out, controlled_buffer_8_out, matmulttile_2x2_1_c1,
       matmulttile_2x2_1_c2, matmulttile_2x2_1_c3, matmulttile_2x2_1_c4, R1_q, R2_q, R3_q, R4_q, ram_1_dout,
       ram_2_dout, RomCPU_data, S1_q, S2_q, S3_q, S4_q;

  Clock clock_1 (.out(clock_1_out));
  or or_1 (or_1_out, RomCPU_data[15], RomCPU_data[14], RomCPU_data[13], in_1);
  RAM #(.dataWidth(16), .\type ("nonvolatile")) ram_1 (
    .addr(counter_1_q), .clk(clock_1_out), .dout(ram_1_dout));  // open: we, oe, din
  Counter counter_1 (
    .load(RomCPU_data[2]), .D(8'h8), .count(or_1_out), .Q(counter_1_q), .clk(clock_1_out),
    .clr(RomCPU_data[1]));  // open: carry, up
  RAM #(.dataWidth(16), .\type ("nonvolatile")) ram_2 (
    .addr(counter_2_q), .clk(clock_1_out), .dout(ram_2_dout));  // open: we, oe, din
  Counter #(.max('hf)) counter_2 (
    .count(or_1_out), .Q(counter_2_q), .clk(clock_1_out));  // open: load, D, carry, up, clr
  // Probe on ram_1_dout
  // Probe on ram_2_dout
  Register #(.width(16)) A1 (.D(ram_1_dout), .en(RomCPU_data[15]), .clk(clock_1_out), .Q(A1_q));  // open: clr
  Register #(.width(16)) A2 (.D(ram_1_dout), .en(RomCPU_data[14]), .clk(clock_1_out), .Q(A2_q));  // open: clr
  Register #(.width(16)) A3 (.D(ram_1_dout), .en(RomCPU_data[13]), .clk(clock_1_out), .Q(A3_q));  // open: clr
  Register #(.width(16)) A4 (.D(ram_1_dout), .en(RomCPU_data[12]), .clk(clock_1_out), .Q(A4_q));  // open: clr
  Register #(.width(16)) B1 (.D(ram_2_dout), .en(RomCPU_data[15]), .clk(clock_1_out), .Q(B1_q));  // open: clr
  Register #(.width(16)) B2 (.D(ram_2_dout), .en(RomCPU_data[14]), .clk(clock_1_out), .Q(B2_q));  // open: clr
  Register #(.width(16)) B3 (.D(ram_2_dout), .en(RomCPU_data[13]), .clk(clock_1_out), .Q(B3_q));  // open: clr
  Register #(.width(16)) B4 (.D(ram_2_dout), .en(RomCPU_data[12]), .clk(clock_1_out), .Q(B4_q));  // open: clr
  // Probe on A1_q
  // Probe on A2_q
  // Probe on A3_q
  // Probe on A4_q
  // Probe on B1_q
  // Probe on B2_q
  // Probe on B3_q
  // Probe on B4_q
  Hex_Digit_Display hex_digit_display_1 (.value(counter_3_q_2));  // open: dp
  Hex_Digit_Display hex_digit_display_2 (.value(counter_3_q));  // open: dp
  matMultTile_2x2 matmulttile_2x2_1 (
    .A1(A1_q), .B1(A2_q), .A2(A3_q), .B3(A4_q), .B2(B1_q), .B4(B2_q), .A3(B3_q), .A4(B4_q),
    .C1(matmulttile_2x2_1_c1), .C2(matmulttile_2x2_1_c2), .C3(matmulttile_2x2_1_c3), .C4(matmulttile_2x2_1_c4));
  // Probe on matmulttile_2x2_1_c4
  Register #(.width(16)) R1 (.D(matmulttile_2x2_1_c1), .en(RomCPU_data[11]), .clk(clock_1_out), .Q(R1_q));  // open: clr
  // Probe on matmulttile_2x2_1_c1
  Register #(.width(16)) R2 (.D(matmulttile_2x2_1_c2), .en(RomCPU_data[11]), .clk(clock_1_out), .Q(R2_q));  // open: clr
  // Probe on matmulttile_2x2_1_c2
  Register #(.width(16)) R3 (.D(matmulttile_2x2_1_c3), .en(RomCPU_data[11]), .clk(clock_1_out), .Q(R3_q));  // open: clr
  // Probe on matmulttile_2x2_1_c3
  Register #(.width(16)) R4 (.D(matmulttile_2x2_1_c4), .en(RomCPU_data[11]), .clk(clock_1_out), .Q(R4_q));  // open: clr
  Register #(.width(16)) S1 (.D(matmulttile_2x2_1_c1), .en(RomCPU_data[10]), .clk(clock_1_out), .Q(S1_q));  // open: clr
  // Probe on matmulttile_2x2_1_c1
  Register #(.width(16)) S2 (.D(matmulttile_2x2_1_c2), .en(RomCPU_data[10]), .clk(clock_1_out), .Q(S2_q));  // open: clr
  // Probe on matmulttile_2x2_1_c2
  Register #(.width(16)) S3 (.D(matmulttile_2x2_1_c3), .en(RomCPU_data[10]), .clk(clock_1_out), .Q(S3_q));  // open: clr
  // Probe on matmulttile_2x2_1_c3
  Register #(.width(16)) S4 (.D(matmulttile_2x2_1_c4), .en(RomCPU_data[10]), .clk(clock_1_out), .Q(S4_q));  // open: clr
  // Probe on matmulttile_2x2_1_c4
  Counter counter_3 (.Q({counter_3_q_2, counter_3_q}), .clk(clock_1_out));  // open: load, D, count, carry, up, clr
  assign controlled_buffer_1_out = RomCPU_data[7] ? R1_q : 16'bz;  // Controlled_Buffer controlled_buffer_1
  assign controlled_buffer_2_out = RomCPU_data[6] ? R2_q : 16'bz;  // Controlled_Buffer controlled_buffer_2
  assign controlled_buffer_3_out = RomCPU_data[5] ? R3_q : 16'bz;  // Controlled_Buffer controlled_buffer_3
  assign controlled_buffer_4_out = RomCPU_data[7] ? S1_q : 16'bz;  // Controlled_Buffer controlled_buffer_4
  assign controlled_buffer_5_out = RomCPU_data[6] ? S2_q : 16'bz;  // Controlled_Buffer controlled_buffer_5
  assign controlled_buffer_6_out = RomCPU_data[5] ? S3_q : 16'bz;  // Controlled_Buffer controlled_buffer_6
  // Probe on controlled_buffer_1_out
  // Probe on controlled_buffer_2_out
  // Probe on controlled_buffer_3_out
  // Probe on controlled_buffer_7_out
  assign controlled_buffer_7_out = RomCPU_data[4] ? R4_q : 16'bz;  // Controlled_Buffer controlled_buffer_7
  // Probe on controlled_buffer_4_out
  // Probe on controlled_buffer_5_out
  // Probe on controlled_buffer_6_out
  // Probe on controlled_buffer_8_out
  assign controlled_buffer_8_out = RomCPU_data[4] ? S4_q : 16'bz;  // Controlled_Buffer controlled_buffer_8
  ROM #(.dataWidth(16)) RomCPU (.addr({counter_3_q_2, counter_3_q}), .data(RomCPU_data));
  Adder #(.width(16)) adder_1 (
    .a(controlled_buffer_1_out), .b(controlled_buffer_4_out), .out(adder_1_out));  // open: cin, cout
  Adder #(.width(16)) adder_2 (
    .a(controlled_buffer_2_out), .b(controlled_buffer_5_out), .out(adder_1_out));  // open: cin, cout
  Adder #(.width(16)) adder_3 (
    .a(controlled_buffer_3_out), .b(controlled_buffer_6_out), .out(adder_1_out));  // open: cin, cout
  Adder #(.width(16)) adder_4 (
    .a(controlled_buffer_7_out), .b(controlled_buffer_8_out), .out(adder_1_out));  // open: cin, cout
  // Probe on adder_1_out
  Counter counter_4 (.count(or_2_out), .Q(counter_4_q), .clk(clock_1_out));  // open: load, D, carry, up, clr
  or or_2 (or_2_out, RomCPU_data[7], RomCPU_data[6], RomCPU_data[5], RomCPU_data[4]);
  RAM #(.dataWidth(16)) ram_3 (
    .addr(counter_4_q), .we(RomCPU_data[0]), .clk(clock_1_out), .din(adder_1_out));  // open: oe, dout

  // Notes on the sheet:
  //   contents of RomCPU (hex, n*v repeats v):
  //   8000 8000 4000 2000 1000 8800 8000 4000 2000 1000 400 81 41 21 11 2 8000 8000 4000 2000 1000 8800
  //   8000 4000 2000 1000 481 41 21 11 8000 8000 4000 2000 1000 8800 4000 2000 1000 400 81 41 21 11 8004
  //   8000 8000 4000 2000 1000 8800 8000 4000 2000 1000 400 81 41 21 11
endmodule

module matMult_gausian (
);

  wire clock_1_out, or_1_out, or_2_out, or_3_out;
  wire [3:0] counter_3_q, counter_3_q_2;
  wire [7:0] counter_1_q, counter_2_q, counter_4_q;
  wire [15:0] A1_q, A2_q, A3_q, A4_q, B1_q, B2_q, B3_q, B4_q, C1_q, controlled_buffer_1_out,
       matmult_4x4_1_element, ram_1_dout, ram_2_dout, rom_1_data;

  or or_1 (or_1_out, rom_1_data[15], rom_1_data[14], rom_1_data[13], rom_1_data[12]);
  Clock clock_1 (.out(clock_1_out));
  or or_2 (or_2_out, rom_1_data[8], rom_1_data[9], rom_1_data[10], rom_1_data[11]);
  RAM #(.dataWidth(16), .\type ("nonvolatile")) ram_1 (
    .addr(counter_1_q), .oe(or_1_out), .clk(clock_1_out), .dout(ram_1_dout));  // open: we, din
  Counter counter_1 (.count(or_1_out), .Q(counter_1_q), .clk(clock_1_out));  // open: load, D, carry, up, clr
  Counter #(.max('hf)) counter_2 (
    .count(or_2_out), .Q(counter_2_q), .clk(clock_1_out));  // open: load, D, carry, up, clr
  RAM #(.dataWidth(16), .\type ("nonvolatile")) ram_2 (
    .addr(counter_2_q), .clk(clock_1_out), .dout(ram_2_dout));  // open: we, oe, din
  // Probe on ram_1_dout
  // Probe on ram_2_dout
  Register #(.width(16)) A1 (.D(ram_1_dout), .en(rom_1_data[15]), .clk(clock_1_out), .Q(A1_q));  // open: clr
  Register #(.width(16)) A2 (.D(ram_1_dout), .en(rom_1_data[14]), .clk(clock_1_out), .Q(A2_q));  // open: clr
  Register #(.width(16)) A3 (.D(ram_1_dout), .en(rom_1_data[13]), .clk(clock_1_out), .Q(A3_q));  // open: clr
  Register #(.width(16)) A4 (.D(ram_1_dout), .en(rom_1_data[12]), .clk(clock_1_out), .Q(A4_q));  // open: clr
  Register #(.width(16)) B1 (.D(ram_2_dout), .en(rom_1_data[11]), .clk(clock_1_out), .Q(B1_q));  // open: clr
  Register #(.width(16)) B2 (.D(ram_2_dout), .en(rom_1_data[10]), .clk(clock_1_out), .Q(B2_q));  // open: clr
  Register #(.width(16)) B3 (.D(ram_2_dout), .en(rom_1_data[9]), .clk(clock_1_out), .Q(B3_q));  // open: clr
  Register #(.width(16)) B4 (.D(ram_2_dout), .en(rom_1_data[8]), .clk(clock_1_out), .Q(B4_q));  // open: clr
  // Probe on A1_q
  // Probe on A2_q
  // Probe on A3_q
  // Probe on A4_q
  // Probe on B1_q
  // Probe on B2_q
  // Probe on B3_q
  // Probe on B4_q
  Hex_Digit_Display hex_digit_display_1 (.value(counter_3_q_2));  // open: dp
  Hex_Digit_Display hex_digit_display_2 (.value(counter_3_q));  // open: dp
  matMult_4x4 matmult_4x4_1 (
    .row1(A1_q), .row2(A2_q), .row3(A3_q), .row4(A4_q), .col1(B1_q), .col2(B2_q), .col3(B3_q), .col4(B4_q),
    .Element(matmult_4x4_1_element));  // open: carryout
  // Probe on matmult_4x4_1_element
  Register #(.width(16)) C1 (.D(matmult_4x4_1_element), .en(rom_1_data[7]), .clk(clock_1_out), .Q(C1_q));  // open: clr
  assign controlled_buffer_1_out = rom_1_data[3] ? C1_q : 16'bz;  // Controlled_Buffer controlled_buffer_1
  ROM #(.dataWidth(16)) rom_1 (.addr({counter_3_q_2, counter_3_q}), .data(rom_1_data));
  Counter counter_3 (.Q({counter_3_q_2, counter_3_q}), .clk(clock_1_out));  // open: load, D, count, carry, up, clr
  // Probe on controlled_buffer_1_out
  or or_3 (or_3_out, rom_1_data[0], rom_1_data[1], rom_1_data[2], rom_1_data[3]);
  RAM #(.dataWidth(16)) ram_3 (
    .addr(counter_4_q), .we(or_3_out), .clk(clock_1_out), .din(controlled_buffer_1_out));  // open: oe, dout
  Counter counter_4 (.count(or_3_out), .Q(counter_4_q), .clk(clock_1_out));  // open: load, D, carry, up, clr
  // Probe on counter_4_q

  // Notes on the sheet:
  //   contents of rom_1 (hex, n*v repeats v):
  //   8800 8800 4400 2200 1100 880 408 200 100 880 408 200 100 880 408 200 100 8880 4408 2200 1100 880 408
  //   200 100 880 408 200 100 880 408 200 100 8880 4408 2200 1100 880 408 200 100 880 408 200 100 880 408
  //   200 100 8880 4408 2200 1100 880 408 200 100 880 408 200 100 880 408 200 100 80 8
endmodule

module sumofsum_auto (
);

  wire clock_1_out, or_1_out;
  wire [7:0] counter_1_q, counter_2_q, counter_3_q, counter_4_q, counter_5_q;
  wire [15:0] A1_q, A2_q, A3_q, A4_q, B1_q, B2_q, B3_q, B4_q, controlled_buffer_1_out,
       controlled_buffer_5_out, multiadder_16bit_1_r1, multiadder_16bit_1_r2, multiadder_16bit_1_r3,
       multiadder_16bit_1_r4, R1_q, R2_q, R3_q, R4_q, ram_1_dout, ram_2_dout, register_1_q, register_2_q,
       register_3_q, register_4_q, register_5_q, rom_1_data, sum_4val_1_result;

  Clock clock_1 (.out(clock_1_out));
  RAM #(.dataWidth(16), .\type ("nonvolatile")) ram_1 (
    .addr(counter_1_q), .clk(clock_1_out), .dout(ram_1_dout));  // open: we, oe, din
  // Probe on counter_1_q
  Counter counter_1 (.Q(counter_1_q), .clk(clock_1_out));  // open: load, D, count, carry, up, clr
  RAM #(.dataWidth(16), .\type ("nonvolatile")) ram_2 (
    .addr(counter_1_q), .clk(clock_1_out), .dout(ram_2_dout));  // open: we, oe, din
  // Probe on ram_1_dout
  // Probe on ram_2_dout
  Register #(.width(16)) A1 (.D(ram_1_dout), .en(rom_1_data[15]), .clk(clock_1_out), .Q(A1_q));  // open: clr
  Register #(.width(16)) A2 (.D(ram_1_dout), .en(rom_1_data[14]), .clk(clock_1_out), .Q(A2_q));  // open: clr
  Register #(.width(16)) A3 (.D(ram_1_dout), .en(rom_1_data[13]), .clk(clock_1_out), .Q(A3_q));  // open: clr
  Register #(.width(16)) A4 (.D(ram_1_dout), .en(rom_1_data[12]), .clk(clock_1_out), .Q(A4_q));  // open: clr
  Register #(.width(16)) B1 (.D(ram_2_dout), .en(rom_1_data[11]), .clk(clock_1_out), .Q(B1_q));  // open: clr
  Register #(.width(16)) B2 (.D(ram_2_dout), .en(rom_1_data[10]), .clk(clock_1_out), .Q(B2_q));  // open: clr
  Register #(.width(16)) B3 (.D(ram_2_dout), .en(rom_1_data[9]), .clk(clock_1_out), .Q(B3_q));  // open: clr
  Register #(.width(16)) B4 (.D(ram_2_dout), .en(rom_1_data[8]), .clk(clock_1_out), .Q(B4_q));  // open: clr
  // Probe on A1_q
  // Probe on A2_q
  // Probe on A3_q
  // Probe on A4_q
  // Probe on B1_q
  // Probe on B2_q
  // Probe on B3_q
  // Probe on B4_q
  multiadder_16bit multiadder_16bit_1 (
    .A1(A1_q), .A2(A2_q), .A3(A3_q), .A4(A4_q), .B1(B1_q), .B2(B2_q), .B3(B3_q), .B4(B4_q),
    .R1(multiadder_16bit_1_r1), .R2(multiadder_16bit_1_r2), .R3(multiadder_16bit_1_r3),
    .R4(multiadder_16bit_1_r4));  // open: C1, C2, C3, C4
  // Probe on multiadder_16bit_1_r1
  // Probe on multiadder_16bit_1_r2
  // Probe on multiadder_16bit_1_r3
  // Probe on multiadder_16bit_1_r4
  Register #(.width(16)) R1 (.D(multiadder_16bit_1_r1), .en(rom_1_data[7]), .clk(clock_1_out), .Q(R1_q));  // open: clr
  Register #(.width(16)) R2 (.D(multiadder_16bit_1_r2), .en(rom_1_data[6]), .clk(clock_1_out), .Q(R2_q));  // open: clr
  Register #(.width(16)) R3 (.D(multiadder_16bit_1_r3), .en(rom_1_data[5]), .clk(clock_1_out), .Q(R3_q));  // open: clr
  Register #(.width(16)) R4 (.D(multiadder_16bit_1_r4), .en(rom_1_data[4]), .clk(clock_1_out), .Q(R4_q));  // open: clr
  assign controlled_buffer_1_out = rom_1_data[3] ? R1_q : 16'bz;  // Controlled_Buffer controlled_buffer_1
  assign controlled_buffer_1_out = rom_1_data[2] ? R2_q : 16'bz;  // Controlled_Buffer controlled_buffer_2
  ROM #(.dataWidth(16)) rom_1 (.addr(counter_2_q), .data(rom_1_data));
  Counter counter_2 (.Q(counter_2_q), .clk(clock_1_out));  // open: load, D, count, carry, up, clr
  assign controlled_buffer_1_out = rom_1_data[1] ? R3_q : 16'bz;  // Controlled_Buffer controlled_buffer_3
  assign controlled_buffer_1_out = rom_1_data[0] ? R4_q : 16'bz;  // Controlled_Buffer controlled_buffer_4
  // Probe on controlled_buffer_1_out
  // Probe on controlled_buffer_1_out
  // Probe on controlled_buffer_1_out
  // Probe on controlled_buffer_1_out
  or or_1 (or_1_out, rom_1_data[0], rom_1_data[1], rom_1_data[2], rom_1_data[3]);
  RAM #(.dataWidth(16)) ram_3 (
    .addr(counter_3_q), .we(or_1_out), .clk(clock_1_out), .din(controlled_buffer_1_out));  // open: oe, dout
  Counter counter_3 (.count(or_1_out), .Q(counter_3_q), .clk(clock_1_out));  // open: load, D, carry, up, clr
  // Probe on counter_3_q
  Register #(.width(16)) register_1 (.D(R1_q), .en(rom_1_data[3]), .clk(rom_1_data[3]), .Q(register_1_q));  // open: clr
  Register #(.width(16)) register_2 (.D(R2_q), .en(rom_1_data[2]), .clk(rom_1_data[2]), .Q(register_2_q));  // open: clr
  Register #(.width(16)) register_3 (.D(R3_q), .en(rom_1_data[1]), .clk(rom_1_data[1]), .Q(register_3_q));  // open: clr
  Register #(.width(16)) register_4 (.D(R4_q), .en(rom_1_data[0]), .clk(rom_1_data[0]), .Q(register_4_q));  // open: clr
  sum_4val sum_4val_1 (
    .sum1(register_1_q), .sum2(register_2_q), .sum3(register_3_q), .sum4(register_4_q),
    .result(sum_4val_1_result));  // open: carry
  Register #(.width(16)) register_5 (
    .D(controlled_buffer_5_out), .en(rom_1_data[0]), .clk(rom_1_data[0]), .Q(register_5_q));  // open: clr
  assign controlled_buffer_5_out = rom_1_data[0] ? sum_4val_1_result : 16'bz;  // Controlled_Buffer controlled_buffer_5
  Counter counter_4 (.Q(counter_4_q), .clk(rom_1_data[3]));  // open: load, D, count, carry, up, clr
  Counter counter_5 (.D(counter_4_q), .Q(counter_5_q), .clk(rom_1_data[3]));  // open: load, count, carry, up, clr
  RAM #(.dataWidth(16)) RamD (
    .addr(counter_5_q), .we(clock_1_out), .clk(clock_1_out), .din(register_5_q));  // open: oe, dout

  // Notes on the sheet:
  //   contents of rom_1 (hex, n*v repeats v):
  //   0 8800 4480 2248 1124 8812 4481
endmodule

module ram2multiadder_auto (
);

  wire clock_1_out, or_1_out, or_2_out;
  wire [3:0] counter_1_q, counter_1_q_2;
  wire [7:0] counter_2_q, counter_3_q;
  wire [15:0] A1_q, A2_q, A3_q, A4_q, B1_q, B2_q, B3_q, B4_q, controlled_buffer_1_out, multiadder_16bit_1_r1,
       multiadder_16bit_1_r2, multiadder_16bit_1_r3, multiadder_16bit_1_r4, R1_q, R2_q, R3_q, R4_q,
       ram_1_dout, ram_2_dout, RomCPU_data;

  or or_1 (or_1_out, RomCPU_data[11], RomCPU_data[10], RomCPU_data[9], RomCPU_data[8]);
  Clock clock_1 (.out(clock_1_out));
  RAM #(.dataWidth(16), .\type ("nonvolatile")) ram_1 (
    .addr({counter_1_q_2, counter_1_q}), .clk(clock_1_out), .dout(ram_1_dout));  // open: we, oe, din
  Counter counter_1 (
    .count(or_1_out), .Q({counter_1_q_2, counter_1_q}), .clk(clock_1_out));  // open: load, D, carry, up, clr
  RAM #(.dataWidth(16), .\type ("nonvolatile")) ram_2 (
    .addr({counter_1_q_2, counter_1_q}), .clk(clock_1_out), .dout(ram_2_dout));  // open: we, oe, din
  // Probe on ram_1_dout
  // Probe on ram_2_dout
  Register #(.width(16)) A1 (.D(ram_1_dout), .en(RomCPU_data[15]), .clk(clock_1_out), .Q(A1_q));  // open: clr
  Register #(.width(16)) A2 (.D(ram_1_dout), .en(RomCPU_data[14]), .clk(clock_1_out), .Q(A2_q));  // open: clr
  Register #(.width(16)) A3 (.D(ram_1_dout), .en(RomCPU_data[13]), .clk(clock_1_out), .Q(A3_q));  // open: clr
  Register #(.width(16)) A4 (.D(ram_1_dout), .en(RomCPU_data[12]), .clk(clock_1_out), .Q(A4_q));  // open: clr
  Register #(.width(16)) B1 (.D(ram_2_dout), .en(RomCPU_data[11]), .clk(clock_1_out), .Q(B1_q));  // open: clr
  Register #(.width(16)) B2 (.D(ram_2_dout), .en(RomCPU_data[10]), .clk(clock_1_out), .Q(B2_q));  // open: clr
  Register #(.width(16)) B3 (.D(ram_2_dout), .en(RomCPU_data[9]), .clk(clock_1_out), .Q(B3_q));  // open: clr
  Register #(.width(16)) B4 (.D(ram_2_dout), .en(RomCPU_data[8]), .clk(clock_1_out), .Q(B4_q));  // open: clr
  // Probe on B1_q
  // Probe on B2_q
  // Probe on A1_q
  // Probe on A2_q
  // Probe on A3_q
  // Probe on A4_q
  // Probe on B3_q
  // Probe on B4_q
  Hex_Digit_Display hex_digit_display_1 (.value(counter_1_q_2));  // open: dp
  Hex_Digit_Display hex_digit_display_2 (.value(counter_1_q));  // open: dp
  multiadder_16bit multiadder_16bit_1 (
    .A1(A1_q), .A2(A2_q), .A3(A3_q), .A4(A4_q), .B1(B1_q), .B2(B2_q), .B3(B3_q), .B4(B4_q),
    .R1(multiadder_16bit_1_r1), .R2(multiadder_16bit_1_r2), .R3(multiadder_16bit_1_r3),
    .R4(multiadder_16bit_1_r4));  // open: C1, C2, C3, C4
  // Probe on multiadder_16bit_1_r1
  // Probe on multiadder_16bit_1_r2
  // Probe on multiadder_16bit_1_r3
  // Probe on multiadder_16bit_1_r4
  Register #(.width(16)) R1 (.D(multiadder_16bit_1_r1), .en(RomCPU_data[7]), .clk(clock_1_out), .Q(R1_q));  // open: clr
  Register #(.width(16)) R2 (.D(multiadder_16bit_1_r2), .en(RomCPU_data[6]), .clk(clock_1_out), .Q(R2_q));  // open: clr
  Register #(.width(16)) R3 (.D(multiadder_16bit_1_r3), .en(RomCPU_data[5]), .clk(clock_1_out), .Q(R3_q));  // open: clr
  Register #(.width(16)) R4 (.D(multiadder_16bit_1_r4), .en(RomCPU_data[4]), .clk(clock_1_out), .Q(R4_q));  // open: clr
  Counter counter_2 (.Q(counter_2_q), .clk(clock_1_out));  // open: load, D, count, carry, up, clr
  assign controlled_buffer_1_out = RomCPU_data[3] ? R1_q : 16'bz;  // Controlled_Buffer controlled_buffer_1
  assign controlled_buffer_1_out = RomCPU_data[2] ? R2_q : 16'bz;  // Controlled_Buffer controlled_buffer_2
  ROM #(.dataWidth(16)) RomCPU (.addr(counter_2_q), .data(RomCPU_data));
  assign controlled_buffer_1_out = RomCPU_data[1] ? R3_q : 16'bz;  // Controlled_Buffer controlled_buffer_3
  assign controlled_buffer_1_out = RomCPU_data[0] ? R4_q : 16'bz;  // Controlled_Buffer controlled_buffer_4
  // Probe on controlled_buffer_1_out
  // Probe on controlled_buffer_1_out
  // Probe on controlled_buffer_1_out
  // Probe on controlled_buffer_1_out
  or or_2 (or_2_out, RomCPU_data[0], RomCPU_data[1], RomCPU_data[2], RomCPU_data[3]);
  Counter counter_3 (.count(or_2_out), .Q(counter_3_q), .clk(clock_1_out));  // open: load, D, carry, up, clr
  // Probe on counter_3_q
  RAM #(.dataWidth(16)) ram_3 (
    .addr(counter_3_q), .we(or_2_out), .clk(clock_1_out), .din(controlled_buffer_1_out));  // open: oe, dout

  // Notes on the sheet:
  //   contents of RomCPU (hex, n*v repeats v):
  //   0 8800 4480 2248 1124 8812 4481
endmodule

module ram2multi_compractor (
);

  wire clock_1_out, comparator_1_eq, comparator_2_eq, comparator_3_eq, comparator_4_eq, comparator_5_eq,
       comparator_6_eq, comparator_7_eq, comparator_8_eq, comparator_9_eq, comparator_10_eq;
  wire [7:0] counter_1_q, counter_2_q, counter_3_q;
  wire [15:0] A1_q, A2_q, A3_q, A4_q, B1_q, B2_q, B3_q, B4_q, controlled_buffer_1_out, multiadder_16bit_1_r1,
       multiadder_16bit_1_r2, multiadder_16bit_1_r3, multiadder_16bit_1_r4, R1_q, R2_q, R3_q, R4_q,
       ram_1_dout, ram_2_dout;

  Clock clock_1 (.out(clock_1_out));
  RAM #(.dataWidth(16), .\type ("nonvolatile")) ram_1 (
    .addr(counter_1_q), .clk(clock_1_out), .dout(ram_1_dout));  // open: we, oe, din
  Counter counter_1 (.Q(counter_1_q), .clk(clock_1_out));  // open: load, D, count, carry, up, clr
  RAM #(.dataWidth(16), .\type ("nonvolatile")) ram_2 (
    .addr(counter_1_q), .clk(clock_1_out), .dout(ram_2_dout));  // open: we, oe, din
  Register #(.width(16)) A1 (.D(ram_1_dout), .en(comparator_2_eq), .clk(clock_1_out), .Q(A1_q));  // open: clr
  Register #(.width(16)) A2 (.D(ram_1_dout), .en(comparator_3_eq), .clk(clock_1_out), .Q(A2_q));  // open: clr
  Register #(.width(16)) A3 (.D(ram_1_dout), .en(comparator_4_eq), .clk(clock_1_out), .Q(A3_q));  // open: clr
  Register #(.width(16)) A4 (.D(ram_1_dout), .en(comparator_5_eq), .clk(clock_1_out), .Q(A4_q));  // open: clr
  Register #(.width(16)) B1 (.D(ram_2_dout), .en(comparator_2_eq), .clk(clock_1_out), .Q(B1_q));  // open: clr
  Register #(.width(16)) B2 (.D(ram_2_dout), .en(comparator_3_eq), .clk(clock_1_out), .Q(B2_q));  // open: clr
  Register #(.width(16)) B3 (.D(ram_2_dout), .en(comparator_4_eq), .clk(clock_1_out), .Q(B3_q));  // open: clr
  Register #(.width(16)) B4 (.D(ram_2_dout), .en(comparator_5_eq), .clk(clock_1_out), .Q(B4_q));  // open: clr
  // Probe on B1_q
  // Probe on B2_q
  // Probe on A1_q
  // Probe on A2_q
  // Probe on A3_q
  // Probe on A4_q
  // Probe on B3_q
  // Probe on B4_q
  Counter counter_2 (.Q(counter_2_q), .clk(clock_1_out), .clr(comparator_1_eq));  // open: load, D, count, carry, up
  Comparator comparator_1 (.a(8'h5), .b(counter_2_q), .eq(comparator_1_eq));  // open: gt, lt
  Comparator comparator_2 (.a(8'h1), .b(counter_2_q), .eq(comparator_2_eq));  // open: gt, lt
  Comparator comparator_3 (.a(8'h2), .b(counter_2_q), .eq(comparator_3_eq));  // open: gt, lt
  Comparator comparator_4 (.a(8'h3), .b(counter_2_q), .eq(comparator_4_eq));  // open: gt, lt
  Comparator comparator_5 (.a(8'h4), .b(counter_2_q), .eq(comparator_5_eq));  // open: gt, lt
  multiadder_16bit multiadder_16bit_1 (
    .A1(A1_q), .A2(A2_q), .A3(A3_q), .A4(A4_q), .B1(B1_q), .B2(B2_q), .B3(B3_q), .B4(B4_q),
    .R1(multiadder_16bit_1_r1), .R2(multiadder_16bit_1_r2), .R3(multiadder_16bit_1_r3),
    .R4(multiadder_16bit_1_r4));  // open: C1, C2, C3, C4
  // Probe on multiadder_16bit_1_r1
  // Probe on multiadder_16bit_1_r2
  // Probe on multiadder_16bit_1_r3
  // Probe on multiadder_16bit_1_r4
  Register #(.width(16)) R1 (.D(multiadder_16bit_1_r1), .clk(clock_1_out), .Q(R1_q));  // open: en, clr
  Register #(.width(16)) R2 (.D(multiadder_16bit_1_r2), .clk(clock_1_out), .Q(R2_q));  // open: en, clr
  Register #(.width(16)) R3 (.D(multiadder_16bit_1_r3), .clk(clock_1_out), .Q(R3_q));  // open: en, clr
  Register #(.width(16)) R4 (.D(multiadder_16bit_1_r4), .clk(clock_1_out), .Q(R4_q));  // open: en, clr
  Comparator comparator_6 (.a(8'h1), .b(counter_3_q), .eq(comparator_6_eq));  // open: gt, lt
  Comparator comparator_7 (.a(8'h2), .b(counter_3_q), .eq(comparator_7_eq));  // open: gt, lt
  Comparator comparator_8 (.a(8'h3), .b(counter_3_q), .eq(comparator_8_eq));  // open: gt, lt
  Comparator comparator_9 (.a(8'h4), .b(counter_3_q), .eq(comparator_9_eq));  // open: gt, lt
  assign controlled_buffer_1_out = comparator_6_eq ? R1_q : 16'bz;  // Controlled_Buffer controlled_buffer_1
  assign controlled_buffer_1_out = comparator_7_eq ? R2_q : 16'bz;  // Controlled_Buffer controlled_buffer_2
  assign controlled_buffer_1_out = comparator_8_eq ? R3_q : 16'bz;  // Controlled_Buffer controlled_buffer_3
  assign controlled_buffer_1_out = comparator_9_eq ? R4_q : 16'bz;  // Controlled_Buffer controlled_buffer_4
  Counter counter_3 (.Q(counter_3_q), .clk(clock_1_out), .clr(comparator_10_eq));  // open: load, D, count, carry, up
  Comparator comparator_10 (.a(8'h3), .b(counter_1_q), .eq(comparator_10_eq));  // open: gt, lt
  RAM #(.dataWidth(16)) ram_3 (
    .addr(counter_1_q), .clk(clock_1_out), .din(controlled_buffer_1_out));  // open: we, oe, dout

  // Notes on the sheet:
  //   Depreciated Aproach
endmodule

module ram2multiAdder_manual (
  input  d,
  input  c,
  input  b,
  input  a,
  input  z,
  input  y,
  input  x,
  input  w,
  input  Pass1,
  input  Pass2,
  input  Pass3,
  input  Pass4
);

  wire clock_1_out, or_1_out;
  wire [7:0] counter_1_q, counter_2_q;
  wire [15:0] A1_q, A2_q, A3_q, A4_q, B1_q, B2_q, B3_q, B4_q, controlled_buffer_1_out, multiadder_16bit_1_r1,
       multiadder_16bit_1_r2, multiadder_16bit_1_r3, multiadder_16bit_1_r4, R1_q, R2_q, R3_q, R4_q,
       ram_1_dout, ram_2_dout;

  Clock clock_1 (.out(clock_1_out));
  RAM #(.dataWidth(16), .\type ("nonvolatile")) ram_1 (
    .addr(counter_1_q), .clk(clock_1_out), .dout(ram_1_dout));  // open: we, oe, din
  Counter counter_1 (.Q(counter_1_q), .clk(clock_1_out));  // open: load, D, count, carry, up, clr
  RAM #(.dataWidth(16), .\type ("nonvolatile")) ram_2 (
    .addr(counter_1_q), .clk(clock_1_out), .dout(ram_2_dout));  // open: we, oe, din
  // Probe on ram_1_dout
  // Probe on ram_2_dout
  Register #(.width(16)) A1 (.D(ram_1_dout), .en(a), .clk(clock_1_out), .Q(A1_q));  // open: clr
  Register #(.width(16)) A2 (.D(ram_1_dout), .en(b), .clk(clock_1_out), .Q(A2_q));  // open: clr
  Register #(.width(16)) A3 (.D(ram_1_dout), .en(c), .clk(clock_1_out), .Q(A3_q));  // open: clr
  Register #(.width(16)) A4 (.D(ram_1_dout), .en(d), .clk(clock_1_out), .Q(A4_q));  // open: clr
  Register #(.width(16)) B1 (.D(ram_2_dout), .en(a), .clk(clock_1_out), .Q(B1_q));  // open: clr
  Register #(.width(16)) B2 (.D(ram_2_dout), .en(b), .clk(clock_1_out), .Q(B2_q));  // open: clr
  Register #(.width(16)) B3 (.D(ram_2_dout), .en(c), .clk(clock_1_out), .Q(B3_q));  // open: clr
  Register #(.width(16)) B4 (.D(ram_2_dout), .en(d), .clk(clock_1_out), .Q(B4_q));  // open: clr
  // Probe on B1_q
  // Probe on B2_q
  // Probe on A1_q
  // Probe on A2_q
  // Probe on A3_q
  // Probe on A4_q
  // Probe on B3_q
  // Probe on B4_q
  multiadder_16bit multiadder_16bit_1 (
    .A1(A1_q), .A2(A2_q), .A3(A3_q), .A4(A4_q), .B1(B1_q), .B2(B2_q), .B3(B3_q), .B4(B4_q),
    .R1(multiadder_16bit_1_r1), .R2(multiadder_16bit_1_r2), .R3(multiadder_16bit_1_r3),
    .R4(multiadder_16bit_1_r4));  // open: C1, C2, C3, C4
  // Probe on multiadder_16bit_1_r2
  // Probe on multiadder_16bit_1_r3
  // Probe on multiadder_16bit_1_r4
  // Probe on multiadder_16bit_1_r1
  Register #(.width(16)) R1 (.D(multiadder_16bit_1_r1), .en(w), .clk(clock_1_out), .Q(R1_q));  // open: clr
  Register #(.width(16)) R2 (.D(multiadder_16bit_1_r2), .en(x), .clk(clock_1_out), .Q(R2_q));  // open: clr
  Register #(.width(16)) R3 (.D(multiadder_16bit_1_r3), .en(y), .clk(clock_1_out), .Q(R3_q));  // open: clr
  Register #(.width(16)) R4 (.D(multiadder_16bit_1_r4), .en(z), .clk(clock_1_out), .Q(R4_q));  // open: clr
  assign controlled_buffer_1_out = Pass1 ? R1_q : 16'bz;  // Controlled_Buffer controlled_buffer_1
  assign controlled_buffer_1_out = Pass2 ? R2_q : 16'bz;  // Controlled_Buffer controlled_buffer_2
  assign controlled_buffer_1_out = Pass3 ? R3_q : 16'bz;  // Controlled_Buffer controlled_buffer_3
  assign controlled_buffer_1_out = Pass4 ? R4_q : 16'bz;  // Controlled_Buffer controlled_buffer_4
  or or_1 (or_1_out, Pass1, Pass2, Pass3, Pass4);
  RAM #(.dataWidth(16)) ram_3 (
    .addr(counter_2_q), .we(or_1_out), .clk(clock_1_out), .din(controlled_buffer_1_out));  // open: oe, dout
  Counter counter_2 (.count(or_1_out), .Q(counter_2_q), .clk(clock_1_out));  // open: load, D, carry, up, clr
endmodule

module ram2Adder_manual (
  input  in_1,
  input  in_2
);

  wire clock_1_out;
  wire [7:0] counter_1_q, counter_2_q;
  wire [15:0] adder_16bit_1_result, ram_1_dout, ram_2_dout, register_1_q, register_2_q, register_3_q;

  Clock clock_1 (.out(clock_1_out));
  // Probe on counter_1_q
  Counter counter_1 (.Q(counter_1_q), .clk(clock_1_out));  // open: load, D, count, carry, up, clr
  RAM #(.dataWidth(16), .\type ("nonvolatile")) ram_1 (
    .addr(counter_1_q), .clk(clock_1_out), .dout(ram_1_dout));  // open: we, oe, din
  RAM #(.dataWidth(16), .\type ("nonvolatile")) ram_2 (
    .addr(counter_1_q), .clk(clock_1_out), .dout(ram_2_dout));  // open: we, oe, din
  // Probe on ram_1_dout
  // Probe on ram_2_dout
  Register #(.width(16)) register_1 (.D(ram_1_dout), .en(in_1), .clk(clock_1_out), .Q(register_1_q));  // open: clr
  Register #(.width(16)) register_2 (.D(ram_2_dout), .en(in_1), .clk(clock_1_out), .Q(register_2_q));  // open: clr
  // Probe on adder_16bit_1_result
  adder_16bit adder_16bit_1 (
    .A(register_1_q), .B(register_2_q), .Result(adder_16bit_1_result));  // open: Carry_in, Carry_out
  Register #(.width(16)) register_3 (.D(adder_16bit_1_result), .clk(clock_1_out), .Q(register_3_q));  // open: en, clr
  RAM #(.dataWidth(16)) ram_3 (.addr(counter_2_q), .we(in_2), .clk(clock_1_out), .din(register_3_q));  // open: oe, dout
  Counter counter_2 (.Q(counter_2_q), .clk(clock_1_out));  // open: load, D, count, carry, up, clr
endmodule

module matmult_systrolicTiling8x8_dep (
);

  wire clock_1_out, or_1_out, or_2_out, undriven_3, undriven_4, undriven_5, undriven_6, undriven_7,
       undriven_8, undriven_9, undriven_10, undriven_11, undriven_12, undriven_13, undriven_14, undriven_15,
       undriven_16;
  wire [3:0] undriven, undriven_2;
  wire [7:0] counter_1_q, counter_2_q, counter_3_q, counter_4_q;
  wire [15:0] A1_q, A2_q, A3_q, A4_q, adder_1_out, adder_2_out, adder_3_out, adder_4_out, B1_q, B2_q, B3_q,
       B4_q, C1_q, C2_q, C3_q, C4_q, C5_q, C6_q, C7_q, C8_q, C9_q, C10_q, C11_q, C12_q, C13_q, C14_q, C15_q,
       C16_q, controlled_buffer_1_out, ram_1_dout, ram_2_dout, ram_3_dout, register_1_q, register_2_q,
       register_3_q, register_4_q, register_5_q, register_6_q, register_7_q, register_8_q, register_9_q,
       systrolic_4x4gausian_1_c1, systrolic_4x4gausian_1_c2, systrolic_4x4gausian_1_c3,
       systrolic_4x4gausian_1_c4, systrolic_4x4gausian_1_c5, systrolic_4x4gausian_1_c6,
       systrolic_4x4gausian_1_c7, systrolic_4x4gausian_1_c8, systrolic_4x4gausian_1_c9,
       systrolic_4x4gausian_1_c10, systrolic_4x4gausian_1_c11, systrolic_4x4gausian_1_c12,
       systrolic_4x4gausian_1_c13, systrolic_4x4gausian_1_c14, systrolic_4x4gausian_1_c15,
       systrolic_4x4gausian_1_c16;
  wire [23:0] rom_1_data;

  or or_1 (or_1_out, rom_1_data[23], rom_1_data[22], rom_1_data[21], rom_1_data[20]);
  Counter counter_1 (.count(or_1_out), .Q(counter_1_q), .clk(clock_1_out));  // open: load, D, carry, up, clr
  Counter counter_2 (.count(or_1_out), .Q(counter_2_q), .clk(clock_1_out));  // open: load, D, carry, up, clr
  Clock clock_1 (.out(clock_1_out));
  RAM #(.dataWidth(16)) ram_1 (.addr(counter_1_q), .clk(clock_1_out), .dout(ram_1_dout));  // open: we, oe, din
  RAM #(.dataWidth(16)) ram_2 (.addr(counter_2_q), .clk(clock_1_out), .dout(ram_2_dout));  // open: we, oe, din
  Register #(.width(16)) A1 (.D(ram_1_dout), .en(rom_1_data[23]), .clk(clock_1_out), .Q(A1_q));  // open: clr
  Register #(.width(16)) A2 (.D(ram_1_dout), .en(rom_1_data[22]), .clk(clock_1_out), .Q(A2_q));  // open: clr
  Register #(.width(16)) A3 (.D(ram_1_dout), .en(rom_1_data[21]), .clk(clock_1_out), .Q(A3_q));  // open: clr
  Register #(.width(16)) A4 (.D(ram_1_dout), .en(rom_1_data[20]), .clk(clock_1_out), .Q(A4_q));  // open: clr
  Register #(.width(16)) B1 (.D(ram_2_dout), .en(rom_1_data[23]), .clk(clock_1_out), .Q(B1_q));  // open: clr
  Register #(.width(16)) B2 (.D(ram_2_dout), .en(rom_1_data[22]), .clk(clock_1_out), .Q(B2_q));  // open: clr
  Register #(.width(16)) B3 (.D(ram_2_dout), .en(rom_1_data[21]), .clk(clock_1_out), .Q(B3_q));  // open: clr
  Register #(.width(16)) B4 (.D(ram_2_dout), .en(rom_1_data[20]), .clk(clock_1_out), .Q(B4_q));  // open: clr
  systrolic_4x4Gausian systrolic_4x4gausian_1 (
    .B1(B1_q), .B2(B2_q), .B3(B3_q), .B4(B4_q), .A1(A1_q), .A2(A2_q), .A3(A3_q), .A4(A4_q),
    .Clock(clock_1_out), .C1(systrolic_4x4gausian_1_c1), .C2(systrolic_4x4gausian_1_c2),
    .C3(systrolic_4x4gausian_1_c3), .C4(systrolic_4x4gausian_1_c4), .C5(systrolic_4x4gausian_1_c5),
    .C6(systrolic_4x4gausian_1_c6), .C7(systrolic_4x4gausian_1_c7), .C8(systrolic_4x4gausian_1_c8),
    .C9(systrolic_4x4gausian_1_c9), .C10(systrolic_4x4gausian_1_c10), .C11(systrolic_4x4gausian_1_c11),
    .C12(systrolic_4x4gausian_1_c12), .C13(systrolic_4x4gausian_1_c13), .C14(systrolic_4x4gausian_1_c14),
    .C15(systrolic_4x4gausian_1_c15), .C16(systrolic_4x4gausian_1_c16));
  Register #(.width(16)) C1 (.D(systrolic_4x4gausian_1_c1), .Q(C1_q));  // open: en, clk, clr
  Register #(.width(16)) C3 (.D(systrolic_4x4gausian_1_c3), .Q(C3_q));  // open: en, clk, clr
  Register #(.width(16)) C5 (.D(systrolic_4x4gausian_1_c5), .Q(C5_q));  // open: en, clk, clr
  Register #(.width(16)) C7 (.D(systrolic_4x4gausian_1_c7), .Q(C7_q));  // open: en, clk, clr
  Register #(.width(16)) C9 (.D(systrolic_4x4gausian_1_c9), .Q(C9_q));  // open: en, clk, clr
  Register #(.width(16)) C11 (.D(systrolic_4x4gausian_1_c11), .Q(C11_q));  // open: en, clk, clr
  Register #(.width(16)) C13 (.D(systrolic_4x4gausian_1_c13), .Q(C13_q));  // open: en, clk, clr
  Register #(.width(16)) C15 (.D(systrolic_4x4gausian_1_c15), .Q(C15_q));  // open: en, clk, clr
  Register #(.width(16)) C2 (.D(systrolic_4x4gausian_1_c2), .Q(C2_q));  // open: en, clk, clr
  Register #(.width(16)) C4 (.D(systrolic_4x4gausian_1_c4), .Q(C4_q));  // open: en, clk, clr
  Register #(.width(16)) C6 (.D(systrolic_4x4gausian_1_c6), .Q(C6_q));  // open: en, clk, clr
  Register #(.width(16)) C8 (.D(systrolic_4x4gausian_1_c8), .Q(C8_q));  // open: en, clk, clr
  Register #(.width(16)) C10 (.D(systrolic_4x4gausian_1_c10), .Q(C10_q));  // open: en, clk, clr
  Register #(.width(16)) C12 (.D(systrolic_4x4gausian_1_c12), .Q(C12_q));  // open: en, clk, clr
  Register #(.width(16)) C14 (.D(systrolic_4x4gausian_1_c14), .Q(C14_q));  // open: en, clk, clr
  Register #(.width(16)) C16 (.D(systrolic_4x4gausian_1_c16), .Q(C16_q));  // open: en, clk, clr
  assign controlled_buffer_1_out = rom_1_data[19] ? C1_q : 16'bz;  // Controlled_Buffer controlled_buffer_1
  assign controlled_buffer_1_out = rom_1_data[18] ? C2_q : 16'bz;  // Controlled_Buffer controlled_buffer_2
  assign controlled_buffer_1_out = rom_1_data[17] ? C3_q : 16'bz;  // Controlled_Buffer controlled_buffer_3
  Hex_Digit_Display hex_digit_display_1 (.value(undriven_2));  // open: dp
  Hex_Digit_Display hex_digit_display_2 (.value(undriven));  // open: dp
  assign controlled_buffer_1_out = rom_1_data[16] ? C4_q : 16'bz;  // Controlled_Buffer controlled_buffer_4
  assign controlled_buffer_1_out = rom_1_data[15] ? C5_q : 16'bz;  // Controlled_Buffer controlled_buffer_5
  assign controlled_buffer_1_out = rom_1_data[14] ? C6_q : 16'bz;  // Controlled_Buffer controlled_buffer_6
  assign controlled_buffer_1_out = rom_1_data[13] ? C7_q : 16'bz;  // Controlled_Buffer controlled_buffer_7
  assign controlled_buffer_1_out = rom_1_data[12] ? C8_q : 16'bz;  // Controlled_Buffer controlled_buffer_8
  assign controlled_buffer_1_out = rom_1_data[11] ? C9_q : 16'bz;  // Controlled_Buffer controlled_buffer_9
  assign controlled_buffer_1_out = rom_1_data[10] ? C10_q : 16'bz;  // Controlled_Buffer controlled_buffer_10
  assign controlled_buffer_1_out = rom_1_data[9] ? C11_q : 16'bz;  // Controlled_Buffer controlled_buffer_11
  assign controlled_buffer_1_out = rom_1_data[8] ? C12_q : 16'bz;  // Controlled_Buffer controlled_buffer_12
  assign controlled_buffer_1_out = rom_1_data[7] ? C13_q : 16'bz;  // Controlled_Buffer controlled_buffer_13
  assign controlled_buffer_1_out = rom_1_data[6] ? C14_q : 16'bz;  // Controlled_Buffer controlled_buffer_14
  assign controlled_buffer_1_out = rom_1_data[5] ? C15_q : 16'bz;  // Controlled_Buffer controlled_buffer_15
  assign controlled_buffer_1_out = rom_1_data[4] ? C16_q : 16'bz;  // Controlled_Buffer controlled_buffer_16
  or or_2 (or_2_out, rom_1_data[4], rom_1_data[5], rom_1_data[6], rom_1_data[7], rom_1_data[8], rom_1_data[9], rom_1_data[10], rom_1_data[11], rom_1_data[12], rom_1_data[13], rom_1_data[14], rom_1_data[15], rom_1_data[16], rom_1_data[17], rom_1_data[18], rom_1_data[19]);
  Counter counter_3 (.Q(counter_3_q), .clk(clock_1_out));  // open: load, D, count, carry, up, clr
  Register #(.width(16)) register_1 (
    .D(controlled_buffer_1_out), .en(or_2_out), .clk(clock_1_out), .Q(register_1_q));  // open: clr
  ROM #(.dataWidth(24)) rom_1 (.addr(counter_3_q), .data(rom_1_data));
  Counter counter_4 (
    .count(rom_1_data[3]), .Q(counter_4_q), .clk(clock_1_out), .clr(undriven_3));  // open: load, D, carry, up
  RAM #(.dataWidth(16)) ram_3 (
    .addr(counter_4_q), .we(rom_1_data[3]), .oe(undriven_4), .clk(clock_1_out), .din(register_1_q),
    .dout(ram_3_dout));
  Register #(.width(16)) register_2 (
    .D(ram_3_dout), .en(undriven_5), .clk(clock_1_out), .Q(register_2_q));  // open: clr
  Register #(.width(16)) register_3 (
    .D(ram_3_dout), .en(undriven_6), .clk(clock_1_out), .Q(register_3_q));  // open: clr
  Register #(.width(16)) register_4 (
    .D(ram_3_dout), .en(undriven_7), .clk(clock_1_out), .Q(register_4_q));  // open: clr
  Register #(.width(16)) register_5 (
    .D(ram_3_dout), .en(undriven_8), .clk(clock_1_out), .Q(register_5_q));  // open: clr
  Register #(.width(16)) register_6 (
    .D(ram_3_dout), .en(undriven_9), .clk(clock_1_out), .Q(register_6_q));  // open: clr
  Register #(.width(16)) register_7 (
    .D(ram_3_dout), .en(undriven_10), .clk(clock_1_out), .Q(register_7_q));  // open: clr
  Register #(.width(16)) register_8 (
    .D(ram_3_dout), .en(undriven_11), .clk(clock_1_out), .Q(register_8_q));  // open: clr
  Register #(.width(16)) register_9 (
    .D(ram_3_dout), .en(undriven_12), .clk(clock_1_out), .Q(register_9_q));  // open: clr
  Adder #(.width(16)) adder_1 (.a(register_2_q), .b(register_6_q), .out(adder_1_out));  // open: cin, cout
  Adder #(.width(16)) adder_2 (.a(register_3_q), .b(register_7_q), .out(adder_2_out));  // open: cin, cout
  Adder #(.width(16)) adder_3 (.a(register_4_q), .b(register_8_q), .out(adder_3_out));  // open: cin, cout
  Adder #(.width(16)) adder_4 (.a(register_5_q), .b(register_9_q), .out(adder_4_out));  // open: cin, cout
  Register #(.width(16)) register_10 (.D(adder_1_out), .en(undriven_13), .clk(clock_1_out));  // open: Q, clr
  Register #(.width(16)) register_11 (.D(adder_2_out), .en(undriven_14), .clk(clock_1_out));  // open: Q, clr
  Register #(.width(16)) register_12 (.D(adder_3_out), .en(undriven_15), .clk(clock_1_out));  // open: Q, clr
  Register #(.width(16)) register_13 (.D(adder_4_out), .en(undriven_16), .clk(clock_1_out));  // open: Q, clr

  // Notes on the sheet:
  //   Not working Invalid aproach!!
endmodule

module Ins_splitter (
  input  [15:0] Instruction,
  input  WE,
  input  Clock,
  output [7:0] Adress,
  output [3:0] Dimension,
  output [3:0] Opcode
);

  Register #(.width(16)) register_1 (
    .D(Instruction), .en(WE), .clk(Clock), .Q({Opcode, Dimension, Adress}));  // open: clr
endmodule

module systrolic_4x4Gausian (
  input  [15:0] B1,
  input  [15:0] B2,
  input  [15:0] B3,
  input  [15:0] B4,
  input  [15:0] A1,
  input  [15:0] A2,
  input  [15:0] A3,
  input  [15:0] A4,
  input  Clock,
  output [15:0] C1,
  output [15:0] C2,
  output [15:0] C3,
  output [15:0] C4,
  output [15:0] C5,
  output [15:0] C6,
  output [15:0] C7,
  output [15:0] C8,
  output [15:0] C9,
  output [15:0] C10,
  output [15:0] C11,
  output [15:0] C12,
  output [15:0] C13,
  output [15:0] C14,
  output [15:0] C15,
  output [15:0] C16
);

  wire [15:0] systrolic_processingelement_1_aout, systrolic_processingelement_1_bout,
       systrolic_processingelement_2_aout, systrolic_processingelement_2_bout,
       systrolic_processingelement_3_aout, systrolic_processingelement_3_bout,
       systrolic_processingelement_4_aout, systrolic_processingelement_5_aout,
       systrolic_processingelement_5_bout, systrolic_processingelement_6_aout,
       systrolic_processingelement_6_bout, systrolic_processingelement_7_aout,
       systrolic_processingelement_7_bout, systrolic_processingelement_8_aout,
       systrolic_processingelement_9_aout, systrolic_processingelement_9_bout,
       systrolic_processingelement_10_aout, systrolic_processingelement_10_bout,
       systrolic_processingelement_11_aout, systrolic_processingelement_11_bout,
       systrolic_processingelement_12_aout, systrolic_processingelement_13_bout,
       systrolic_processingelement_14_bout, systrolic_processingelement_15_bout;

  Systrolic_ProcessingElement systrolic_processingelement_1 (
    .Ain(A1), .Bin(B1), .Clock(Clock), .Aout(systrolic_processingelement_1_aout),
    .Bout(systrolic_processingelement_1_bout), .Cout(C1));
  Systrolic_ProcessingElement systrolic_processingelement_2 (
    .Ain(A2), .Bin(systrolic_processingelement_1_bout), .Clock(Clock),
    .Aout(systrolic_processingelement_2_aout), .Bout(systrolic_processingelement_2_bout), .Cout(C5));
  Systrolic_ProcessingElement systrolic_processingelement_3 (
    .Ain(A3), .Bin(systrolic_processingelement_2_bout), .Clock(Clock),
    .Aout(systrolic_processingelement_3_aout), .Bout(systrolic_processingelement_3_bout), .Cout(C9));
  Systrolic_ProcessingElement systrolic_processingelement_4 (
    .Ain(A4), .Bin(systrolic_processingelement_3_bout), .Clock(Clock),
    .Aout(systrolic_processingelement_4_aout), .Cout(C13));  // open: Bout
  Systrolic_ProcessingElement systrolic_processingelement_5 (
    .Ain(systrolic_processingelement_1_aout), .Bin(B2), .Clock(Clock),
    .Aout(systrolic_processingelement_5_aout), .Bout(systrolic_processingelement_5_bout), .Cout(C2));
  Systrolic_ProcessingElement systrolic_processingelement_6 (
    .Ain(systrolic_processingelement_2_aout), .Bin(systrolic_processingelement_5_bout), .Clock(Clock),
    .Aout(systrolic_processingelement_6_aout), .Bout(systrolic_processingelement_6_bout), .Cout(C6));
  Systrolic_ProcessingElement systrolic_processingelement_7 (
    .Ain(systrolic_processingelement_3_aout), .Bin(systrolic_processingelement_6_bout), .Clock(Clock),
    .Aout(systrolic_processingelement_7_aout), .Bout(systrolic_processingelement_7_bout), .Cout(C10));
  Systrolic_ProcessingElement systrolic_processingelement_8 (
    .Ain(systrolic_processingelement_4_aout), .Bin(systrolic_processingelement_7_bout), .Clock(Clock),
    .Aout(systrolic_processingelement_8_aout), .Cout(C14));  // open: Bout
  Systrolic_ProcessingElement systrolic_processingelement_9 (
    .Ain(systrolic_processingelement_5_aout), .Bin(B3), .Clock(Clock),
    .Aout(systrolic_processingelement_9_aout), .Bout(systrolic_processingelement_9_bout), .Cout(C3));
  Systrolic_ProcessingElement systrolic_processingelement_10 (
    .Ain(systrolic_processingelement_6_aout), .Bin(systrolic_processingelement_9_bout), .Clock(Clock),
    .Aout(systrolic_processingelement_10_aout), .Bout(systrolic_processingelement_10_bout), .Cout(C7));
  Systrolic_ProcessingElement systrolic_processingelement_11 (
    .Ain(systrolic_processingelement_7_aout), .Bin(systrolic_processingelement_10_bout), .Clock(Clock),
    .Aout(systrolic_processingelement_11_aout), .Bout(systrolic_processingelement_11_bout), .Cout(C11));
  Systrolic_ProcessingElement systrolic_processingelement_12 (
    .Ain(systrolic_processingelement_8_aout), .Bin(systrolic_processingelement_11_bout), .Clock(Clock),
    .Aout(systrolic_processingelement_12_aout), .Cout(C15));  // open: Bout
  Systrolic_ProcessingElement systrolic_processingelement_13 (
    .Ain(systrolic_processingelement_9_aout), .Bin(B4), .Clock(Clock),
    .Bout(systrolic_processingelement_13_bout), .Cout(C4));  // open: Aout
  Systrolic_ProcessingElement systrolic_processingelement_14 (
    .Ain(systrolic_processingelement_10_aout), .Bin(systrolic_processingelement_13_bout), .Clock(Clock),
    .Bout(systrolic_processingelement_14_bout), .Cout(C8));  // open: Aout
  Systrolic_ProcessingElement systrolic_processingelement_15 (
    .Ain(systrolic_processingelement_11_aout), .Bin(systrolic_processingelement_14_bout), .Clock(Clock),
    .Bout(systrolic_processingelement_15_bout), .Cout(C12));  // open: Aout
  Systrolic_ProcessingElement systrolic_processingelement_16 (
    .Ain(systrolic_processingelement_12_aout), .Bin(systrolic_processingelement_15_bout), .Clock(Clock),
    .Cout(C16));  // open: Aout, Bout
endmodule

module Systrolic_ProcessingElement (
  input  [15:0] Ain,
  input  [15:0] Bin,
  input  Clock,
  output [15:0] Aout,
  output [15:0] Bout,
  output [15:0] Cout
);

  wire [15:0] adder_1_out, multiplier_1_out;

  Multiplier #(.width(16)) multiplier_1 (.a(Ain), .b(Bin), .out(multiplier_1_out));  // open: cin, cout
  Register #(.trigger("falling"), .width(16)) register_1 (.D(Ain), .en(1'b1), .clk(Clock), .Q(Aout));  // open: clr
  Register #(.trigger("falling"), .width(16)) register_2 (.D(Bin), .en(1'b1), .clk(Clock), .Q(Bout));  // open: clr
  Register #(.trigger("falling"), .width(16)) register_3 (
    .D(adder_1_out), .en(1'b1), .clk(Clock), .Q(Cout));  // open: clr
  Adder #(.width(16)) adder_1 (.a(multiplier_1_out), .b(Cout), .out(adder_1_out));  // open: cin, cout
endmodule

module matMultTile_2x2 (
  input  [15:0] A1,
  input  [15:0] B1,
  input  [15:0] A2,
  input  [15:0] B3,
  input  [15:0] B2,
  input  [15:0] B4,
  input  [15:0] A3,
  input  [15:0] A4,
  output [15:0] C1,
  output [15:0] C2,
  output [15:0] C3,
  output [15:0] C4
);

  wire [15:0] multiplier_1_out, multiplier_2_out, multiplier_3_out, multiplier_4_out, multiplier_5_out,
       multiplier_6_out, multiplier_7_out, multiplier_8_out;

  Multiplier #(.width(16)) multiplier_1 (.a(A1), .b(B1), .out(multiplier_1_out));  // open: cin, cout
  Multiplier #(.width(16)) multiplier_2 (.a(A2), .b(B3), .out(multiplier_2_out));  // open: cin, cout
  Multiplier #(.width(16)) multiplier_3 (.a(A1), .b(B2), .out(multiplier_3_out));  // open: cin, cout
  Multiplier #(.width(16)) multiplier_4 (.a(A2), .b(B4), .out(multiplier_4_out));  // open: cin, cout
  Multiplier #(.width(16)) multiplier_5 (.a(A3), .b(B1), .out(multiplier_5_out));  // open: cin, cout
  Multiplier #(.width(16)) multiplier_6 (.a(A4), .b(B3), .out(multiplier_6_out));  // open: cin, cout
  Multiplier #(.width(16)) multiplier_7 (.a(A3), .b(B2), .out(multiplier_7_out));  // open: cin, cout
  Multiplier #(.width(16)) multiplier_8 (.a(A4), .b(A4), .out(multiplier_8_out));  // open: cin, cout
  Adder #(.width(16)) adder_1 (.a(multiplier_1_out), .b(multiplier_2_out), .out(C1));  // open: cin, cout
  Adder #(.width(16)) adder_2 (.a(multiplier_3_out), .b(multiplier_4_out), .out(C2));  // open: cin, cout
  Adder #(.width(16)) adder_3 (.a(multiplier_5_out), .b(multiplier_6_out), .out(C3));  // open: cin, cout
  Adder #(.width(16)) adder_4 (.a(multiplier_7_out), .b(multiplier_8_out), .out(C4));  // open: cin, cout
endmodule

module matMult_4x4 (
  input  [15:0] row1,
  input  [15:0] row2,
  input  [15:0] row3,
  input  [15:0] row4,
  input  [15:0] col1,
  input  [15:0] col2,
  input  [15:0] col3,
  input  [15:0] col4,
  output [15:0] Element,
  output carryout
);

  wire [15:0] adder_1_out, adder_2_out, multiplier_1_out, multiplier_2_out, multiplier_3_out,
       multiplier_4_out;

  Multiplier #(.width(16)) multiplier_1 (.a(row1), .b(col1), .out(multiplier_1_out));  // open: cin, cout
  Multiplier #(.width(16)) multiplier_2 (.a(row2), .b(col2), .out(multiplier_2_out));  // open: cin, cout
  Multiplier #(.width(16)) multiplier_3 (.a(row3), .b(col3), .out(multiplier_3_out));  // open: cin, cout
  Multiplier #(.width(16)) multiplier_4 (.a(row4), .b(col4), .out(multiplier_4_out));  // open: cin, cout
  Adder #(.width(16)) adder_1 (.a(multiplier_1_out), .b(multiplier_2_out), .out(adder_1_out));  // open: cin, cout
  Adder #(.width(16)) adder_2 (.a(multiplier_3_out), .b(multiplier_4_out), .out(adder_2_out));  // open: cin, cout
  Adder #(.width(16)) adder_3 (.a(adder_1_out), .b(adder_2_out), .out(Element), .cout(carryout));  // open: cin
endmodule

module adder_16bit (
  input  Carry_in,
  input  [15:0] A,
  input  [15:0] B,
  output [15:0] Result,
  output Carry_out
);

  wire adder_8bit_1_carry_out;

  // Probe on A
  // Probe on B
  // Probe on Result
  adder_8bit adder_8bit_1 (
    .Carry_in(Carry_in), .A(A[7:0]), .B(B[7:0]), .Result(Result[7:0]), .Carry_out(adder_8bit_1_carry_out));
  adder_8bit adder_8bit_2 (
    .Carry_in(adder_8bit_1_carry_out), .A(A[15:8]), .B(B[15:8]), .Result(Result[15:8]), .Carry_out(Carry_out));
  // Probe on Carry_out
endmodule

module multiadder_16bit (
  input  [15:0] A1,
  input  [15:0] A2,
  input  [15:0] A3,
  input  [15:0] A4,
  input  [15:0] B1,
  input  [15:0] B2,
  input  [15:0] B3,
  input  [15:0] B4,
  output [15:0] R1,
  output [15:0] R2,
  output [15:0] R3,
  output [15:0] R4,
  output C1,
  output C2,
  output C3,
  output C4
);

  adder_16bit adder_16bit_1 (.A(A1), .B(B1), .Result(R1), .Carry_out(C1));  // open: Carry_in
  adder_16bit adder_16bit_2 (.A(A2), .B(B2), .Result(R2), .Carry_out(C2));  // open: Carry_in
  adder_16bit adder_16bit_3 (.A(A3), .B(B3), .Result(R3), .Carry_out(C3));  // open: Carry_in
  adder_16bit adder_16bit_4 (.A(A4), .B(B4), .Result(R4), .Carry_out(C4));  // open: Carry_in
endmodule

module sum_4val (
  input  [15:0] sum1,
  input  [15:0] sum2,
  input  [15:0] sum3,
  input  [15:0] sum4,
  output [15:0] result,
  output carry
);

  wire [15:0] adder_16bit_1_result, adder_16bit_2_result;

  adder_16bit adder_16bit_1 (.A(sum1), .B(sum2), .Result(adder_16bit_1_result));  // open: Carry_in, Carry_out
  adder_16bit adder_16bit_2 (.A(sum3), .B(sum4), .Result(adder_16bit_2_result));  // open: Carry_in, Carry_out
  adder_16bit adder_16bit_3 (
    .A(adder_16bit_1_result), .B(adder_16bit_2_result), .Result(result), .Carry_out(carry));  // open: Carry_in
endmodule

module adder_32bit (
  input  Carry_in,
  input  [31:0] First_Value,
  input  [31:0] Second_Value,
  output [31:0] Result,
  output Carry_out
);

  wire adder_8bit_1_carry_out, adder_8bit_2_carry_out, adder_8bit_3_carry_out;

  // Probe on First_Value
  // Probe on Second_Value
  // Probe on Carry_in
  adder_8bit adder_8bit_1 (
    .Carry_in(Carry_in), .A(First_Value[7:0]), .B(Second_Value[23:16]), .Result(Result[7:0]),
    .Carry_out(adder_8bit_1_carry_out));
  adder_8bit adder_8bit_2 (
    .Carry_in(adder_8bit_1_carry_out), .A(First_Value[15:8]), .B(Second_Value[15:8]), .Result(Result[15:8]),
    .Carry_out(adder_8bit_2_carry_out));
  adder_8bit adder_8bit_3 (
    .Carry_in(adder_8bit_2_carry_out), .A(First_Value[23:16]), .B(Second_Value[7:0]), .Result(Result[23:16]),
    .Carry_out(adder_8bit_3_carry_out));
  adder_8bit adder_8bit_4 (
    .Carry_in(adder_8bit_3_carry_out), .A(First_Value[31:24]), .B(Second_Value[31:24]),
    .Result(Result[31:24]), .Carry_out(Carry_out));
  // Probe on Result
endmodule

module adder_8bit (
  input  Carry_in,
  input  [7:0] A,
  input  [7:0] B,
  output [7:0] Result,
  output Carry_out
);

  wire adder_4bit_1_out_5;

  // Probe on A
  // Probe on B
  adder_4bit adder_4bit_1 (
    .in_1(Carry_in), .in_2(A[3:0]), .in_3(B[3:0]), .out_4(Result[3:0]), .out_5(adder_4bit_1_out_5));
  adder_4bit adder_4bit_2 (
    .in_1(adder_4bit_1_out_5), .in_2(A[7:4]), .in_3(B[7:4]), .out_4(Result[7:4]), .out_5(Carry_out));
  // Probe on Result
  // Probe on Carry_out
endmodule

module adder_4bit (
  input  in_1,
  input  [3:0] in_2,
  input  [3:0] in_3,
  output [3:0] out_4,
  output out_5
);

  wire adder_2bit_1_out_5;

  // Probe on in_2
  // Probe on in_3
  adder_2bit adder_2bit_1 (
    .InitialCarry(in_1), .A(in_2[1:0]), .B(in_3[1:0]), .sum(out_4[1:0]), .out_5(adder_2bit_1_out_5));
  adder_2bit adder_2bit_2 (
    .InitialCarry(adder_2bit_1_out_5), .A(in_2[3:2]), .B(in_3[3:2]), .sum(out_4[3:2]), .out_5(out_5));
  // Probe on out_4
  // Probe on out_5
endmodule

module adder_2bit (
  input  InitialCarry,
  input  [1:0] A,
  input  [1:0] B,
  output [1:0] sum,
  output out_5
);

  wire adder_1bit_1_carry_out;

  adder_1bit adder_1bit_1 (
    .A(A[0]), .B(B[0]), .Carry_in(InitialCarry), .Sum(sum[0]), .Carry_out(adder_1bit_1_carry_out));
  // Probe on sum
  adder_1bit adder_1bit_2 (.A(A[1]), .B(B[1]), .Carry_in(adder_1bit_1_carry_out), .Sum(sum[1]), .Carry_out(out_5));
endmodule

module adder_1bit (
  input  A,
  input  B,
  input  Carry_in,
  output Sum,
  output Carry_out
);

  wire and_1_out, and_2_out, xor_1_out;

  xor xor_1 (xor_1_out, A, B);
  and and_1 (and_1_out, A, B);
  xor xor_2 (Sum, xor_1_out, Carry_in);
  and and_2 (and_2_out, xor_1_out, Carry_in);
  or or_1 (Carry_out, and_2_out, and_1_out);
endmodule

module test_tiling (
  input  in_1,
  input  [7:0] in_2
);

  wire clock_1_out, clock_2_out;
  wire [3:0] rom_1_data;
  wire [7:0] counter_1_q, counter_2_q, counter_3_q;
  wire [15:0] ram_1_dout, ram_2_dout;

  ROM #(.dataWidth(4)) rom_1 (.addr(counter_1_q), .data(rom_1_data));
  Counter counter_1 (.Q(counter_1_q), .clk(clock_1_out));  // open: load, D, count, carry, up, clr
  Clock clock_1 (.out(clock_1_out));
  Counter #(.max('hf)) counter_2 (
    .count(rom_1_data[3]), .Q(counter_2_q), .clk(clock_1_out));  // open: load, D, carry, up, clr
  Counter #(.max('hf)) counter_3 (
    .load(rom_1_data[1]), .D(8'h8), .count(rom_1_data[2]), .Q(counter_3_q), .clk(clock_1_out),
    .clr(rom_1_data[0]));  // open: carry, up
  RAM #(.dataWidth(16)) ram_1 (.addr(counter_2_q), .clk(clock_1_out), .dout(ram_1_dout));  // open: we, oe, din
  RAM #(.dataWidth(16)) ram_2 (.addr(counter_3_q), .clk(clock_1_out), .dout(ram_2_dout));  // open: we, oe, din
  // Probe on ram_1_dout
  // Probe on ram_2_dout
  Clock clock_2 (.out(clock_2_out));
  Counter counter_4 (.load(in_1), .D(in_2), .clk(clock_2_out));  // open: count, Q, carry, up, clr

  // Notes on the sheet:
  //   contents of rom_1 (hex, n*v repeats v):
  //   8*c 1 15*c e 8*c
  //   Test Case for seeing how to use counters in normal tiling 
endmodule

module registerBanks_4 (
  input  [15:0] value,
  input  WE1,
  input  WE2,
  input  WE3,
  input  WE4,
  input  clock,
  input  reset,
  output [15:0] out1,
  output [15:0] out2,
  output [15:0] out3,
  output [15:0] out4
);

  Register #(.width(16)) register_1 (.D(value), .en(WE1), .clk(clock), .Q(out1), .clr(reset));
  Register #(.width(16)) register_2 (.D(value), .en(WE2), .clk(clock), .Q(out2), .clr(reset));
  Register #(.width(16)) register_3 (.D(value), .en(WE3), .clk(clock), .Q(out3), .clr(reset));
  Register #(.width(16)) register_4 (.D(value), .en(WE4), .clk(clock), .Q(out4), .clr(reset));
endmodule
